// Logisim project Circuit.circ as structural Verilog: 1 circuit, main circuit main
module main (
  input  On_Off_Indicator_2,
  input  On_Off_Indicator_3,
  input  in_3,
  input  in_4,
  input  On_Off_Indicator_4,
  input  On_Off_Indicator_5A,
  input  On_Off_Indicator_5B,
  input  in_8,
  input  in_9,
  input  On_Off_Indicator_Final,
  input  in_11
);

  wire and_1_out, and_2_out, and_3_out, and_4_out, and_5_out, and_6_out, and_7_out, and_8_out, and_9_out,
       and_10_out, and_11_out, and_12_out, and_13_out, and_14_out, and_15_out, and_16_out, and_17_out,
       and_18_out, and_19_out, and_20_out, and_21_out, and_22_out, and_23_out, and_24_out, and_25_out,
       and_26_out, and_27_out, and_28_out, and_29_out, and_30_out, and_31_out, and_32_out, and_33_out,
       and_34_out, and_35_out, and_36_out, and_37_out, and_38_out, and_39_out, and_40_out, and_41_out,
       and_42_out, and_43_out, and_44_out, and_45_out, and_46_out, and_47_out, and_48_out, and_49_out,
       and_50_out, and_51_out, and_52_out, and_53_out, and_54_out, and_55_out, and_56_out, and_57_out,
       and_58_out, and_59_out, and_60_out, and_61_out, and_62_out, and_63_out, and_64_out, and_65_out,
       and_66_out, and_67_out, and_68_out, and_69_out, and_70_out, and_71_out, and_72_out, and_73_out,
       and_74_out, and_75_out, and_76_out, and_77_out, and_78_out, and_79_out, and_80_out, and_81_out,
       and_82_out, and_83_out, and_84_out, and_85_out, and_86_out, and_87_out, and_88_out, and_89_out,
       and_90_out, and_91_out, and_92_out, and_93_out, and_94_out, and_95_out, and_96_out, and_97_out,
       and_98_out, and_99_out, and_100_out, and_101_out, and_102_out, and_103_out, and_104_out, and_105_out,
       and_106_out, and_107_out, and_108_out, and_109_out, and_110_out, and_111_out, and_112_out,
       and_113_out, and_114_out, and_115_out, and_116_out, and_117_out, and_118_out, and_119_out,
       and_120_out, and_121_out, and_122_out, and_123_out, and_124_out, and_125_out, and_126_out,
       and_127_out, and_128_out, and_129_out, and_130_out, and_131_out, and_132_out, and_133_out,
       and_134_out, and_135_out, and_136_out, and_137_out, and_138_out, and_139_out, and_140_out,
       and_141_out, and_142_out, and_143_out, and_144_out, and_145_out, and_146_out, and_147_out,
       and_148_out, and_149_out, and_150_out, and_151_out, and_152_out, and_153_out, and_154_out,
       and_155_out, and_156_out, and_157_out, and_158_out, and_159_out, and_160_out, and_161_out,
       and_162_out, and_163_out, and_164_out, and_165_out, and_166_out, and_167_out, and_168_out,
       and_169_out, and_170_out, and_171_out, and_172_out, and_173_out, and_174_out, and_175_out,
       and_176_out, and_177_out, and_178_out, and_179_out, and_180_out, and_181_out, and_182_out,
       and_183_out, and_184_out, and_185_out, and_186_out, d_ff_1_q, d_ff_2_q, d_ff_3_q, d_ff_3_qn, d_ff_4_q,
       d_ff_4_qn, d_ff_5_q, d_ff_6_q, d_ff_7_q, d_ff_8_q, d_ff_9_q, d_ff_10_q, d_ff_11_q, d_ff_12_q,
       d_ff_13_q, d_ff_14_q, d_ff_15_q, d_ff_16_q, d_ff_17_q, d_ff_18_q, d_ff_19_q, d_ff_20_q, d_ff_21_q,
       d_ff_22_q, d_ff_23_q, d_ff_24_q, d_ff_25_q, d_ff_26_q, d_ff_27_q, d_ff_28_q, d_ff_29_q, d_ff_30_q,
       d_ff_31_q, d_ff_32_q, d_ff_33_q, d_ff_34_q, d_ff_35_q, d_ff_36_q, d_ff_37_q, d_ff_38_q, d_ff_39_q,
       d_ff_40_q, d_ff_41_q, d_ff_42_q, d_ff_43_q, d_ff_44_q, d_ff_45_q, j_k_ff_1_q, j_k_ff_1_qn,
       j_k_ff_2_qn, j_k_ff_3_qn, j_k_ff_4_q, j_k_ff_4_qn, j_k_ff_5_qn, j_k_ff_6_qn, j_k_ff_7_qn, j_k_ff_8_qn,
       j_k_ff_9_qn, j_k_ff_10_qn, j_k_ff_13_qn, j_k_ff_14_qn, j_k_ff_15_qn, j_k_ff_16_qn, j_k_ff_19_qn,
       j_k_ff_20_qn, j_k_ff_21_qn, j_k_ff_22_qn, j_k_ff_23_qn, j_k_ff_24_qn, j_k_ff_25_qn, j_k_ff_26_qn,
       j_k_ff_29_qn, j_k_ff_30_qn, j_k_ff_31_qn, j_k_ff_32_qn, Next_Track_5A_out, Next_Track_5B_out,
       Next_Track_Final_out, Next_Track_out, not_1_out, not_2_out, not_3_out, not_4_out, not_5_out,
       not_6_out, not_7_out, not_8_out, not_9_out, not_10_out, not_11_out, not_12_out, not_13_out,
       not_14_out, not_15_out, not_16_out, not_17_out, not_18_out, not_19_out, not_20_out, not_21_out,
       not_22_out, not_23_out, not_24_out, not_25_out, not_26_out, not_27_out, not_28_out, not_29_out,
       not_30_out, not_31_out, not_32_out, not_33_out, not_34_out, not_35_out, not_36_out, not_37_out,
       not_38_out, not_39_out, not_40_out, not_41_out, not_42_out, not_43_out, not_44_out, not_45_out,
       not_46_out, not_47_out, not_48_out, not_49_out, not_50_out, not_51_out, not_52_out, not_53_out,
       not_54_out, not_55_out, not_56_out, not_57_out, not_58_out, not_59_out, not_60_out, not_61_out,
       not_62_out, or_1_out, or_2_out, or_3_out, or_4_out, or_5_out, or_6_out, or_7_out, or_8_out, or_9_out,
       or_10_out, or_11_out, or_12_out, or_13_out, or_14_out, or_15_out, or_16_out, or_17_out, or_18_out,
       or_19_out, or_20_out, or_21_out, or_22_out, or_23_out, or_24_out, or_25_out, or_26_out, or_27_out,
       or_28_out, or_29_out, or_30_out, or_31_out, or_32_out, or_33_out, or_34_out, or_35_out, or_36_out,
       or_37_out, or_38_out, or_39_out, or_40_out, or_41_out, or_42_out, or_43_out, or_44_out, or_45_out,
       or_46_out, or_47_out, or_48_out, or_49_out, or_50_out, or_51_out, or_52_out, or_53_out, or_54_out,
       or_55_out, or_56_out, or_57_out, or_58_out, or_59_out, or_60_out, or_61_out, or_62_out, or_63_out,
       or_64_out, or_65_out, or_66_out, or_67_out, or_68_out, or_69_out, or_70_out, or_71_out, or_72_out,
       or_73_out, or_74_out, or_75_out, or_76_out, or_77_out, or_78_out, or_79_out, or_80_out, or_81_out,
       or_82_out, or_83_out, or_84_out, or_85_out, or_86_out, or_87_out, or_88_out, or_89_out, or_90_out,
       or_91_out, or_92_out, Pause_Button1A_out, Pause_Button1B_out, Play_Button1A_out, Play_Button1B_out,
       Play_Pause_Button_4_out, Play_Pause_Button_Final_out, Previous_Track_5A_out, Previous_Track_5B_out,
       Previous_Track_Final_out, Previous_Track_out, undriven, Volume_Down_5A_out, Volume_Down_5B_out,
       Volume_Down_Final_out, Volume_Down_out, Volume_Up_5A_out, Volume_Up_5B_out, Volume_Up_Final_out,
       Volume_Up_out, xnor_1_out, xnor_2_out, xnor_3_out, xnor_4_out;
  wire [3:0] j_k_ff_2_q, j_k_ff_3_q, j_k_ff_9_q, j_k_ff_10_q, j_k_ff_19_q, j_k_ff_20_q, j_k_ff_23_q,
       j_k_ff_24_q;

  Button Play_Button1B (.out(Play_Button1B_out));
  Button Pause_Button1B (.out(Pause_Button1B_out));
  Button Play_Button1A (.out(Play_Button1A_out));
  Button Pause_Button1A (.out(Pause_Button1A_out));
  Button Play_Pause_Button_4 (.out(Play_Pause_Button_4_out));
  D_Flip_Flop d_ff_1 (.D(Play_Button1B_out), .clk(Play_Button1B_out), .Q(d_ff_1_q));  // open: Qn, preset, reset
  and and_1 (and_1_out, d_ff_1_q, Pause_Button1B_out);
  J_K_Flip_Flop j_k_ff_1 (
    .J(On_Off_Indicator_4), .K(Play_Pause_Button_4_out), .clk(Play_Pause_Button_4_out), .Q(j_k_ff_1_q),
    .Qn(j_k_ff_1_qn), .reset(not_1_out));  // open: preset
  Button Volume_Up_5A (.out(Volume_Up_5A_out));
  Button Volume_Down_5A (.out(Volume_Down_5A_out));
  Button Next_Track_5A (.out(Next_Track_5A_out));
  Button Previous_Track_5A (.out(Previous_Track_5A_out));
  D_Flip_Flop d_ff_2 (.D(Play_Button1A_out), .clk(Play_Button1A_out), .Q(d_ff_2_q));  // open: Qn, preset, reset
  D_Flip_Flop d_ff_3 (
    .D(Play_Button1A_out), .clk(Play_Button1A_out), .Q(d_ff_3_q), .Qn(d_ff_3_qn), .reset(and_2_out));  // open: preset
  and and_2 (and_2_out, d_ff_2_q, Pause_Button1A_out);
  D_Flip_Flop d_ff_4 (
    .D(Play_Button1B_out), .clk(Play_Button1B_out), .Q(d_ff_4_q), .Qn(d_ff_4_qn), .preset(d_ff_5_q),
    .reset(and_1_out));
  not not_1 (not_1_out, On_Off_Indicator_4);
  and and_3 (and_3_out, d_ff_4_qn, d_ff_1_q);
  and and_4 (and_4_out, On_Off_Indicator_4, j_k_ff_1_q);
  and and_5 (and_5_out, j_k_ff_1_qn, On_Off_Indicator_4);
  and and_6 (and_6_out, On_Off_Indicator_5A, Volume_Up_5A_out);
  and and_7 (and_7_out, On_Off_Indicator_5A, Volume_Down_5A_out);
  and and_8 (and_8_out, d_ff_3_qn, d_ff_2_q);
  D_Flip_Flop d_ff_5 (.D(undriven), .clk(Pause_Button1B_out), .Q(d_ff_5_q));  // open: Qn, preset, reset
  LED Play_LED_1A (.in(d_ff_3_q));
  LED Pause_LED_1A (.in(and_8_out));
  LED Play_LED_1B (.in(d_ff_4_q));
  LED Pause_LED_1B (.in(and_3_out));
  LED Play_LED (.in(and_4_out));
  LED Pause_LED (.in(and_5_out));
  D_Flip_Flop d_ff_6 (.Q(d_ff_6_q), .preset(and_6_out), .reset(and_7_out));  // open: D, clk, Qn
  or or_1 (or_1_out, and_80_out, and_108_out);
  D_Flip_Flop d_ff_7 (.Q(d_ff_7_q), .preset(Next_Track_5A_out), .reset(Previous_Track_5A_out));  // open: D, clk, Qn
  or or_2 (or_2_out, Next_Track_5A_out, Previous_Track_5A_out);
  not not_2 (not_2_out, d_ff_6_q);
  not not_3 (not_3_out, or_46_out);
  not not_4 (not_4_out, d_ff_7_q);
  and and_9 (and_9_out, On_Off_Indicator_5A, d_ff_6_q);
  and and_10 (and_10_out, not_2_out, d_ff_9_q);
  and and_11 (and_11_out, d_ff_8_q, d_ff_6_q);
  and and_12 (and_12_out, not_2_out, d_ff_10_q);
  and and_13 (and_13_out, d_ff_9_q, d_ff_6_q);
  and and_14 (and_14_out, not_2_out, d_ff_11_q);
  and and_15 (and_15_out, d_ff_10_q, d_ff_6_q);
  and and_16 (and_16_out, not_2_out, d_ff_12_q);
  and and_17 (and_17_out, d_ff_11_q, d_ff_6_q);
  and and_18 (and_18_out, not_2_out, d_ff_13_q);
  and and_19 (and_19_out, d_ff_12_q, d_ff_6_q);
  and and_20 (and_20_out, not_2_out, d_ff_14_q);
  and and_21 (and_21_out, d_ff_13_q, d_ff_6_q);
  and and_22 (and_22_out, not_2_out, d_ff_15_q);
  and and_23 (and_23_out, d_ff_14_q, d_ff_6_q);
  and and_24 (and_24_out, not_2_out, in_8);
  and and_25 (and_25_out, not_3_out, not_4_out);
  xnor xnor_1 (xnor_1_out, and_6_out, and_7_out);
  or or_3 (or_3_out, and_9_out, and_10_out);
  or or_4 (or_4_out, and_11_out, and_12_out);
  or or_5 (or_5_out, and_13_out, and_14_out);
  or or_6 (or_6_out, and_15_out, and_16_out);
  or or_7 (or_7_out, and_17_out, and_18_out);
  or or_8 (or_8_out, and_19_out, and_20_out);
  or or_9 (or_9_out, and_21_out, and_22_out);
  or or_10 (or_10_out, and_23_out, and_24_out);
  J_K_Flip_Flop #(.trigger("falling")) j_k_ff_2 (
    .J(On_Off_Indicator_5A), .K(On_Off_Indicator_5A), .clk(or_2_out), .Q(j_k_ff_2_q[0]), .Qn(j_k_ff_2_qn),
    .preset(or_1_out), .reset(and_79_out));
  J_K_Flip_Flop #(.trigger("falling")) j_k_ff_3 (
    .J(On_Off_Indicator_5A), .K(On_Off_Indicator_5A), .clk(or_11_out), .Q(j_k_ff_3_q[0]), .Qn(j_k_ff_3_qn),
    .reset(and_80_out));  // open: preset
  or or_11 (or_11_out, and_87_out, and_25_out);
  D_Flip_Flop d_ff_8 (.D(or_3_out), .clk(xnor_1_out), .Q(d_ff_8_q));  // open: Qn, preset, reset
  D_Flip_Flop d_ff_9 (.D(or_4_out), .clk(xnor_1_out), .Q(d_ff_9_q));  // open: Qn, preset, reset
  D_Flip_Flop d_ff_10 (.D(or_5_out), .clk(xnor_1_out), .Q(d_ff_10_q));  // open: Qn, preset, reset
  D_Flip_Flop d_ff_11 (.D(or_6_out), .clk(xnor_1_out), .Q(d_ff_11_q));  // open: Qn, preset, reset
  D_Flip_Flop d_ff_12 (.D(or_7_out), .clk(xnor_1_out), .Q(d_ff_12_q));  // open: Qn, preset, reset
  D_Flip_Flop d_ff_13 (.D(or_8_out), .clk(xnor_1_out), .Q(d_ff_13_q));  // open: Qn, preset, reset
  D_Flip_Flop d_ff_14 (.D(or_9_out), .clk(xnor_1_out), .Q(d_ff_14_q));  // open: Qn, preset, reset
  D_Flip_Flop d_ff_15 (.D(or_10_out), .clk(xnor_1_out), .Q(d_ff_15_q));  // open: Qn, preset, reset
  not not_5 (not_5_out, d_ff_7_q);
  not not_6 (not_6_out, d_ff_7_q);
  Button Play_Pause_Button_Final (.out(Play_Pause_Button_Final_out));
  Button Volume_Up_Final (.out(Volume_Up_Final_out));
  Button Volume_Down_Final (.out(Volume_Down_Final_out));
  Button Next_Track_Final (.out(Next_Track_Final_out));
  Button Previous_Track_Final (.out(Previous_Track_Final_out));
  and and_26 (and_26_out, d_ff_7_q, j_k_ff_2_q[0]);
  and and_27 (and_27_out, j_k_ff_2_qn, not_5_out);
  and and_28 (and_28_out, d_ff_7_q, j_k_ff_3_q[0]);
  and and_29 (and_29_out, j_k_ff_3_qn, not_6_out);
  Button Volume_Up (.out(Volume_Up_out));
  Button Volume_Down (.out(Volume_Down_out));
  or or_12 (or_12_out, and_26_out, and_27_out);
  or or_13 (or_13_out, and_28_out, and_29_out);
  J_K_Flip_Flop j_k_ff_4 (
    .J(On_Off_Indicator_Final), .K(Play_Pause_Button_Final_out), .clk(Play_Pause_Button_Final_out),
    .Q(j_k_ff_4_q), .Qn(j_k_ff_4_qn), .reset(not_7_out));  // open: preset
  not not_7 (not_7_out, On_Off_Indicator_Final);
  D_Flip_Flop d_ff_16 (.Q(d_ff_16_q), .preset(Volume_Up_out), .reset(Volume_Down_out));  // open: D, clk, Qn
  J_K_Flip_Flop #(.trigger("falling")) j_k_ff_5 (
    .J(or_12_out), .K(or_12_out), .clk(or_2_out), .Q(j_k_ff_2_q[1]), .Qn(j_k_ff_5_qn), .reset(or_14_out));  // open: preset
  or or_14 (or_14_out, and_83_out, and_79_out);
  J_K_Flip_Flop #(.trigger("falling")) j_k_ff_6 (
    .J(or_13_out), .K(or_13_out), .clk(or_11_out), .Q(j_k_ff_3_q[1]), .Qn(j_k_ff_6_qn), .reset(or_15_out));  // open: preset
  or or_15 (or_15_out, and_84_out, and_80_out);
  and and_30 (and_30_out, On_Off_Indicator_Final, Volume_Up_Final_out);
  and and_31 (and_31_out, On_Off_Indicator_Final, Volume_Down_Final_out);
  not not_8 (not_8_out, d_ff_16_q);
  and and_32 (and_32_out, and_26_out, j_k_ff_2_q[1]);
  and and_33 (and_33_out, j_k_ff_5_qn, and_27_out);
  and and_34 (and_34_out, and_28_out, j_k_ff_3_q[1]);
  and and_35 (and_35_out, j_k_ff_6_qn, and_29_out);
  and and_36 (and_36_out, On_Off_Indicator_Final, j_k_ff_4_q);
  and and_37 (and_37_out, j_k_ff_4_qn, On_Off_Indicator_Final);
  or or_16 (or_16_out, and_110_out, and_122_out);
  and and_38 (and_38_out, in_4, d_ff_16_q);
  and and_39 (and_39_out, not_8_out, d_ff_20_q);
  and and_40 (and_40_out, d_ff_19_q, d_ff_16_q);
  and and_41 (and_41_out, not_8_out, d_ff_21_q);
  and and_42 (and_42_out, d_ff_20_q, d_ff_16_q);
  and and_43 (and_43_out, not_8_out, d_ff_22_q);
  and and_44 (and_44_out, d_ff_21_q, d_ff_16_q);
  and and_45 (and_45_out, not_8_out, d_ff_23_q);
  and and_46 (and_46_out, d_ff_22_q, d_ff_16_q);
  and and_47 (and_47_out, not_8_out, d_ff_24_q);
  and and_48 (and_48_out, d_ff_23_q, d_ff_16_q);
  and and_49 (and_49_out, not_8_out, d_ff_25_q);
  and and_50 (and_50_out, d_ff_24_q, d_ff_16_q);
  and and_51 (and_51_out, not_8_out, d_ff_26_q);
  and and_52 (and_52_out, d_ff_25_q, d_ff_16_q);
  and and_53 (and_53_out, not_8_out, in_3);
  D_Flip_Flop d_ff_17 (.Q(d_ff_17_q), .preset(and_30_out), .reset(and_31_out));  // open: D, clk, Qn
  D_Flip_Flop d_ff_18 (
    .Q(d_ff_18_q), .preset(Next_Track_Final_out), .reset(Previous_Track_Final_out));  // open: D, clk, Qn
  or or_17 (or_17_out, Next_Track_Final_out, Previous_Track_Final_out);
  xnor xnor_2 (xnor_2_out, Volume_Up_out, Volume_Down_out);
  or or_18 (or_18_out, and_38_out, and_39_out);
  or or_19 (or_19_out, and_40_out, and_41_out);
  or or_20 (or_20_out, and_42_out, and_43_out);
  or or_21 (or_21_out, and_44_out, and_45_out);
  or or_22 (or_22_out, and_46_out, and_47_out);
  or or_23 (or_23_out, and_48_out, and_49_out);
  or or_24 (or_24_out, and_50_out, and_51_out);
  or or_25 (or_25_out, and_52_out, and_53_out);
  J_K_Flip_Flop #(.trigger("falling")) j_k_ff_7 (
    .J(or_26_out), .K(or_26_out), .clk(or_2_out), .Q(j_k_ff_2_q[2]), .Qn(j_k_ff_7_qn), .reset(or_27_out));  // open: preset
  or or_26 (or_26_out, and_32_out, and_33_out);
  or or_27 (or_27_out, and_83_out, and_79_out);
  J_K_Flip_Flop #(.trigger("falling")) j_k_ff_8 (
    .J(or_28_out), .K(or_28_out), .clk(or_11_out), .Q(j_k_ff_3_q[2]), .Qn(j_k_ff_8_qn), .reset(or_29_out));  // open: preset
  or or_28 (or_28_out, and_34_out, and_35_out);
  or or_29 (or_29_out, and_84_out, and_80_out);
  not not_9 (not_9_out, d_ff_17_q);
  not not_10 (not_10_out, or_54_out);
  not not_11 (not_11_out, d_ff_18_q);
  D_Flip_Flop d_ff_19 (.D(or_18_out), .clk(xnor_2_out), .Q(d_ff_19_q));  // open: Qn, preset, reset
  D_Flip_Flop d_ff_20 (.D(or_19_out), .clk(xnor_2_out), .Q(d_ff_20_q));  // open: Qn, preset, reset
  D_Flip_Flop d_ff_21 (.D(or_20_out), .clk(xnor_2_out), .Q(d_ff_21_q));  // open: Qn, preset, reset
  D_Flip_Flop d_ff_22 (.D(or_21_out), .clk(xnor_2_out), .Q(d_ff_22_q));  // open: Qn, preset, reset
  D_Flip_Flop d_ff_23 (.D(or_22_out), .clk(xnor_2_out), .Q(d_ff_23_q));  // open: Qn, preset, reset
  D_Flip_Flop d_ff_24 (.D(or_23_out), .clk(xnor_2_out), .Q(d_ff_24_q));  // open: Qn, preset, reset
  D_Flip_Flop d_ff_25 (.D(or_24_out), .clk(xnor_2_out), .Q(d_ff_25_q));  // open: Qn, preset, reset
  D_Flip_Flop d_ff_26 (.D(or_25_out), .clk(xnor_2_out), .Q(d_ff_26_q));  // open: Qn, preset, reset
  and and_54 (and_54_out, On_Off_Indicator_Final, d_ff_17_q);
  and and_55 (and_55_out, not_9_out, d_ff_28_q);
  and and_56 (and_56_out, d_ff_27_q, d_ff_17_q);
  and and_57 (and_57_out, not_9_out, d_ff_29_q);
  and and_58 (and_58_out, d_ff_28_q, d_ff_17_q);
  and and_59 (and_59_out, not_9_out, d_ff_30_q);
  and and_60 (and_60_out, d_ff_29_q, d_ff_17_q);
  and and_61 (and_61_out, not_9_out, d_ff_31_q);
  and and_62 (and_62_out, d_ff_30_q, d_ff_17_q);
  and and_63 (and_63_out, not_9_out, d_ff_32_q);
  and and_64 (and_64_out, d_ff_31_q, d_ff_17_q);
  and and_65 (and_65_out, not_9_out, d_ff_33_q);
  and and_66 (and_66_out, d_ff_32_q, d_ff_17_q);
  and and_67 (and_67_out, not_9_out, d_ff_34_q);
  and and_68 (and_68_out, d_ff_33_q, d_ff_17_q);
  and and_69 (and_69_out, not_9_out, in_11);
  and and_70 (and_70_out, not_10_out, not_11_out);
  and and_71 (and_71_out, and_32_out, j_k_ff_2_q[2]);
  and and_72 (and_72_out, j_k_ff_7_qn, and_33_out);
  and and_73 (and_73_out, and_34_out, j_k_ff_3_q[2]);
  and and_74 (and_74_out, j_k_ff_8_qn, and_35_out);
  xnor xnor_3 (xnor_3_out, and_30_out, and_31_out);
  or or_30 (or_30_out, and_54_out, and_55_out);
  or or_31 (or_31_out, and_56_out, and_57_out);
  or or_32 (or_32_out, and_58_out, and_59_out);
  or or_33 (or_33_out, and_60_out, and_61_out);
  or or_34 (or_34_out, and_62_out, and_63_out);
  or or_35 (or_35_out, and_64_out, and_65_out);
  or or_36 (or_36_out, and_66_out, and_67_out);
  or or_37 (or_37_out, and_68_out, and_69_out);
  J_K_Flip_Flop #(.trigger("falling")) j_k_ff_9 (
    .J(On_Off_Indicator_Final), .K(On_Off_Indicator_Final), .clk(or_17_out), .Q(j_k_ff_9_q[0]),
    .Qn(j_k_ff_9_qn), .preset(or_16_out), .reset(and_109_out));
  J_K_Flip_Flop #(.trigger("falling")) j_k_ff_10 (
    .J(On_Off_Indicator_Final), .K(On_Off_Indicator_Final), .clk(or_38_out), .Q(j_k_ff_10_q[0]),
    .Qn(j_k_ff_10_qn), .reset(and_110_out));  // open: preset
  or or_38 (or_38_out, and_113_out, and_70_out);
  or or_39 (or_39_out, and_71_out, and_72_out);
  or or_40 (or_40_out, and_73_out, and_74_out);
  D_Flip_Flop d_ff_27 (.D(or_30_out), .clk(xnor_3_out), .Q(d_ff_27_q));  // open: Qn, preset, reset
  D_Flip_Flop d_ff_28 (.D(or_31_out), .clk(xnor_3_out), .Q(d_ff_28_q));  // open: Qn, preset, reset
  D_Flip_Flop d_ff_29 (.D(or_32_out), .clk(xnor_3_out), .Q(d_ff_29_q));  // open: Qn, preset, reset
  D_Flip_Flop d_ff_30 (.D(or_33_out), .clk(xnor_3_out), .Q(d_ff_30_q));  // open: Qn, preset, reset
  D_Flip_Flop d_ff_31 (.D(or_34_out), .clk(xnor_3_out), .Q(d_ff_31_q));  // open: Qn, preset, reset
  D_Flip_Flop d_ff_32 (.D(or_35_out), .clk(xnor_3_out), .Q(d_ff_32_q));  // open: Qn, preset, reset
  D_Flip_Flop d_ff_33 (.D(or_36_out), .clk(xnor_3_out), .Q(d_ff_33_q));  // open: Qn, preset, reset
  D_Flip_Flop d_ff_34 (.D(or_37_out), .clk(xnor_3_out), .Q(d_ff_34_q));  // open: Qn, preset, reset
  not not_12 (not_12_out, d_ff_18_q);
  not not_13 (not_13_out, d_ff_18_q);
  J_K_Flip_Flop #(.trigger("falling")) j_k_ff_11 (
    .J(or_39_out), .K(or_39_out), .clk(or_2_out), .Q(j_k_ff_2_q[3]), .preset(and_108_out), .reset(and_79_out));  // open: Qn
  J_K_Flip_Flop #(.trigger("falling")) j_k_ff_12 (
    .J(or_40_out), .K(or_40_out), .clk(or_11_out), .Q(j_k_ff_3_q[3]), .reset(and_80_out));  // open: Qn, preset
  and and_75 (and_75_out, d_ff_18_q, j_k_ff_9_q[0]);
  and and_76 (and_76_out, j_k_ff_9_qn, not_12_out);
  and and_77 (and_77_out, d_ff_18_q, j_k_ff_10_q[0]);
  and and_78 (and_78_out, j_k_ff_10_qn, not_13_out);
  not not_14 (not_14_out, j_k_ff_2_q[2]);
  not not_15 (not_15_out, j_k_ff_2_q[0]);
  and and_79 (and_79_out, j_k_ff_2_q[3], not_14_out, d_ff_7_q, not_15_out, j_k_ff_2_q[1]);
  and and_80 (and_80_out, j_k_ff_3_q[3], d_ff_7_q, j_k_ff_3_q[1]);
  or or_41 (or_41_out, and_75_out, and_76_out);
  or or_42 (or_42_out, and_77_out, and_78_out);
  and and_81 (and_81_out, d_ff_19_q, On_Off_Indicator_2);
  and and_82 (and_82_out, d_ff_20_q, On_Off_Indicator_2);
  and and_83 (and_83_out, j_k_ff_2_q[3], j_k_ff_2_q[1], j_k_ff_2_q[0]);
  or or_43 (or_43_out, j_k_ff_3_q[1], j_k_ff_3_q[2]);
  and and_84 (and_84_out, j_k_ff_3_q[3], or_43_out, j_k_ff_3_q[0]);
  J_K_Flip_Flop #(.trigger("falling")) j_k_ff_13 (
    .J(or_41_out), .K(or_41_out), .clk(or_17_out), .Q(j_k_ff_9_q[1]), .Qn(j_k_ff_13_qn), .reset(or_44_out));  // open: preset
  or or_44 (or_44_out, and_111_out, and_109_out);
  J_K_Flip_Flop #(.trigger("falling")) j_k_ff_14 (
    .J(or_42_out), .K(or_42_out), .clk(or_38_out), .Q(j_k_ff_10_q[1]), .Qn(j_k_ff_14_qn), .reset(or_45_out));  // open: preset
  or or_45 (or_45_out, and_112_out, and_110_out);
  LedBar ledbar_1 (
    .led0(and_81_out), .led1(and_82_out), .led2(and_85_out), .led3(and_86_out), .led4(and_92_out),
    .led5(and_93_out), .led6(and_94_out), .led7(and_95_out));
  and and_85 (and_85_out, d_ff_21_q, On_Off_Indicator_2);
  and and_86 (and_86_out, d_ff_22_q, On_Off_Indicator_2);
  and and_87 (and_87_out, j_k_ff_2_q[0], d_ff_7_q, j_k_ff_2_q[3]);
  and and_88 (and_88_out, and_75_out, j_k_ff_9_q[1]);
  and and_89 (and_89_out, j_k_ff_13_qn, and_76_out);
  and and_90 (and_90_out, and_77_out, j_k_ff_10_q[1]);
  and and_91 (and_91_out, j_k_ff_14_qn, and_78_out);
  and and_92 (and_92_out, d_ff_23_q, On_Off_Indicator_2);
  and and_93 (and_93_out, d_ff_24_q, On_Off_Indicator_2);
  and and_94 (and_94_out, d_ff_25_q, On_Off_Indicator_2);
  or or_46 (or_46_out, j_k_ff_2_q[0], j_k_ff_2_q[1], j_k_ff_2_q[2], j_k_ff_2_q[3]);
  and and_95 (and_95_out, d_ff_26_q, On_Off_Indicator_2);
  and and_96 (and_96_out, On_Off_Indicator_5A, d_ff_8_q);
  and and_97 (and_97_out, On_Off_Indicator_5A, d_ff_9_q);
  and and_98 (and_98_out, On_Off_Indicator_5A, d_ff_10_q);
  J_K_Flip_Flop #(.trigger("falling")) j_k_ff_15 (
    .J(or_47_out), .K(or_47_out), .clk(or_17_out), .Q(j_k_ff_9_q[2]), .Qn(j_k_ff_15_qn), .reset(or_48_out));  // open: preset
  or or_47 (or_47_out, and_88_out, and_89_out);
  or or_48 (or_48_out, and_111_out, and_109_out);
  J_K_Flip_Flop #(.trigger("falling")) j_k_ff_16 (
    .J(or_49_out), .K(or_49_out), .clk(or_38_out), .Q(j_k_ff_10_q[2]), .Qn(j_k_ff_16_qn), .reset(or_50_out));  // open: preset
  or or_49 (or_49_out, and_90_out, and_91_out);
  or or_50 (or_50_out, and_112_out, and_110_out);
  LedBar VOLUME_5A (
    .led0(and_96_out), .led1(and_97_out), .led2(and_98_out), .led3(and_99_out), .led4(and_100_out),
    .led5(and_101_out), .led6(and_102_out), .led7(and_103_out));
  and and_99 (and_99_out, On_Off_Indicator_5A, d_ff_11_q);
  and and_100 (and_100_out, On_Off_Indicator_5A, d_ff_12_q);
  Hex_Digit_Display TRACK_5A (.value(j_k_ff_3_q));  // open: dp
  Hex_Digit_Display hex_digit_display_1 (.value(j_k_ff_2_q));  // open: dp
  and and_101 (and_101_out, On_Off_Indicator_5A, d_ff_13_q);
  and and_102 (and_102_out, On_Off_Indicator_5A, d_ff_14_q);
  and and_103 (and_103_out, On_Off_Indicator_5A, d_ff_15_q);
  and and_104 (and_104_out, and_88_out, j_k_ff_9_q[2]);
  and and_105 (and_105_out, j_k_ff_15_qn, and_89_out);
  and and_106 (and_106_out, and_90_out, j_k_ff_10_q[2]);
  and and_107 (and_107_out, j_k_ff_16_qn, and_91_out);
  J_K_Flip_Flop #(.trigger("falling")) j_k_ff_17 (
    .J(or_51_out), .K(or_51_out), .clk(or_17_out), .Q(j_k_ff_9_q[3]), .preset(and_122_out),
    .reset(and_109_out));  // open: Qn
  or or_51 (or_51_out, and_104_out, and_105_out);
  J_K_Flip_Flop #(.trigger("falling")) j_k_ff_18 (
    .J(or_52_out), .K(or_52_out), .clk(or_38_out), .Q(j_k_ff_10_q[3]), .reset(and_110_out));  // open: Qn, preset
  or or_52 (or_52_out, and_106_out, and_107_out);
  and and_108 (and_108_out, not_16_out, not_17_out, not_18_out, not_19_out, not_20_out, not_21_out, not_22_out, not_23_out);
  not not_16 (not_16_out, j_k_ff_2_q[0]);
  not not_17 (not_17_out, j_k_ff_2_q[1]);
  not not_18 (not_18_out, j_k_ff_2_q[2]);
  not not_19 (not_19_out, j_k_ff_2_q[3]);
  not not_20 (not_20_out, j_k_ff_3_q[0]);
  not not_21 (not_21_out, j_k_ff_3_q[1]);
  not not_22 (not_22_out, j_k_ff_3_q[2]);
  not not_23 (not_23_out, j_k_ff_3_q[3]);
  not not_24 (not_24_out, j_k_ff_9_q[2]);
  not not_25 (not_25_out, j_k_ff_9_q[0]);
  and and_109 (and_109_out, j_k_ff_9_q[3], not_24_out, d_ff_18_q, not_25_out, j_k_ff_9_q[1]);
  and and_110 (and_110_out, j_k_ff_10_q[3], d_ff_18_q, j_k_ff_10_q[1]);
  and and_111 (and_111_out, j_k_ff_9_q[3], j_k_ff_9_q[1], j_k_ff_9_q[0]);
  or or_53 (or_53_out, j_k_ff_10_q[1], j_k_ff_10_q[2]);
  and and_112 (and_112_out, j_k_ff_10_q[3], or_53_out, j_k_ff_10_q[0]);
  and and_113 (and_113_out, j_k_ff_9_q[0], d_ff_18_q, j_k_ff_9_q[3]);
  LED Play_LED_Final (.in(and_36_out));
  LED Pause_LED_Final (.in(and_37_out));
  and and_114 (and_114_out, On_Off_Indicator_Final, d_ff_27_q);
  or or_54 (or_54_out, j_k_ff_9_q[0], j_k_ff_9_q[1], j_k_ff_9_q[2], j_k_ff_9_q[3]);
  LedBar VOLUME (
    .led0(and_114_out), .led1(and_115_out), .led2(and_116_out), .led3(and_117_out), .led4(and_118_out),
    .led5(and_119_out), .led6(and_120_out), .led7(and_121_out));
  and and_115 (and_115_out, On_Off_Indicator_Final, d_ff_28_q);
  and and_116 (and_116_out, On_Off_Indicator_Final, d_ff_29_q);
  Hex_Digit_Display TRACK (.value(j_k_ff_10_q));  // open: dp
  and and_117 (and_117_out, On_Off_Indicator_Final, d_ff_30_q);
  and and_118 (and_118_out, On_Off_Indicator_Final, d_ff_31_q);
  and and_119 (and_119_out, On_Off_Indicator_Final, d_ff_32_q);
  Hex_Digit_Display hex_digit_display_2 (.value(j_k_ff_9_q));  // open: dp
  Button Next_Track (.out(Next_Track_out));
  Button Previous_Track (.out(Previous_Track_out));
  and and_120 (and_120_out, On_Off_Indicator_Final, d_ff_33_q);
  and and_121 (and_121_out, On_Off_Indicator_Final, d_ff_34_q);
  or or_55 (or_55_out, and_164_out, and_176_out);
  D_Flip_Flop d_ff_35 (.Q(d_ff_35_q), .preset(Next_Track_out), .reset(Previous_Track_out));  // open: D, clk, Qn
  or or_56 (or_56_out, Next_Track_out, Previous_Track_out);
  not not_26 (not_26_out, or_88_out);
  not not_27 (not_27_out, d_ff_35_q);
  and and_122 (and_122_out, not_28_out, not_29_out, not_30_out, not_31_out, not_32_out, not_33_out, not_34_out, not_35_out);
  and and_123 (and_123_out, not_26_out, not_27_out);
  Button Volume_Up_5B (.out(Volume_Up_5B_out));
  Button Volume_Down_5B (.out(Volume_Down_5B_out));
  Button Next_Track_5B (.out(Next_Track_5B_out));
  Button Previous_Track_5B (.out(Previous_Track_5B_out));
  not not_28 (not_28_out, j_k_ff_9_q[0]);
  not not_29 (not_29_out, j_k_ff_9_q[1]);
  not not_30 (not_30_out, j_k_ff_9_q[2]);
  not not_31 (not_31_out, j_k_ff_9_q[3]);
  not not_32 (not_32_out, j_k_ff_10_q[0]);
  not not_33 (not_33_out, j_k_ff_10_q[1]);
  not not_34 (not_34_out, j_k_ff_10_q[2]);
  not not_35 (not_35_out, j_k_ff_10_q[3]);
  or or_57 (or_57_out, and_167_out, and_123_out);
  J_K_Flip_Flop #(.trigger("falling")) j_k_ff_19 (
    .J(On_Off_Indicator_3), .K(On_Off_Indicator_3), .clk(or_56_out), .Q(j_k_ff_19_q[0]), .Qn(j_k_ff_19_qn),
    .preset(or_55_out), .reset(and_163_out));
  J_K_Flip_Flop #(.trigger("falling")) j_k_ff_20 (
    .J(On_Off_Indicator_3), .K(On_Off_Indicator_3), .clk(or_57_out), .Q(j_k_ff_20_q[0]), .Qn(j_k_ff_20_qn),
    .reset(and_164_out));  // open: preset
  not not_36 (not_36_out, d_ff_35_q);
  not not_37 (not_37_out, d_ff_35_q);
  and and_124 (and_124_out, On_Off_Indicator_5B, Volume_Up_5B_out);
  and and_125 (and_125_out, On_Off_Indicator_5B, Volume_Down_5B_out);
  and and_126 (and_126_out, d_ff_35_q, j_k_ff_19_q[0]);
  and and_127 (and_127_out, j_k_ff_19_qn, not_36_out);
  and and_128 (and_128_out, d_ff_35_q, j_k_ff_20_q[0]);
  and and_129 (and_129_out, j_k_ff_20_qn, not_37_out);
  J_K_Flip_Flop #(.trigger("falling")) j_k_ff_21 (
    .J(or_58_out), .K(or_58_out), .clk(or_56_out), .Q(j_k_ff_19_q[1]), .Qn(j_k_ff_21_qn), .reset(or_62_out));  // open: preset
  or or_58 (or_58_out, and_126_out, and_127_out);
  J_K_Flip_Flop #(.trigger("falling")) j_k_ff_22 (
    .J(or_59_out), .K(or_59_out), .clk(or_57_out), .Q(j_k_ff_20_q[1]), .Qn(j_k_ff_22_qn), .reset(or_63_out));  // open: preset
  or or_59 (or_59_out, and_128_out, and_129_out);
  D_Flip_Flop d_ff_36 (.Q(d_ff_36_q), .preset(and_124_out), .reset(and_125_out));  // open: D, clk, Qn
  or or_60 (or_60_out, and_173_out, and_186_out);
  D_Flip_Flop d_ff_37 (.Q(d_ff_37_q), .preset(Next_Track_5B_out), .reset(Previous_Track_5B_out));  // open: D, clk, Qn
  or or_61 (or_61_out, Next_Track_5B_out, Previous_Track_5B_out);
  or or_62 (or_62_out, and_165_out, and_163_out);
  or or_63 (or_63_out, and_166_out, and_164_out);
  not not_38 (not_38_out, d_ff_36_q);
  not not_39 (not_39_out, or_92_out);
  not not_40 (not_40_out, d_ff_37_q);
  and and_130 (and_130_out, and_126_out, j_k_ff_19_q[1]);
  and and_131 (and_131_out, j_k_ff_21_qn, and_127_out);
  and and_132 (and_132_out, and_128_out, j_k_ff_20_q[1]);
  and and_133 (and_133_out, j_k_ff_22_qn, and_129_out);
  and and_134 (and_134_out, On_Off_Indicator_5B, d_ff_36_q);
  and and_135 (and_135_out, not_38_out, d_ff_39_q);
  and and_136 (and_136_out, d_ff_38_q, d_ff_36_q);
  and and_137 (and_137_out, not_38_out, d_ff_40_q);
  and and_138 (and_138_out, d_ff_39_q, d_ff_36_q);
  and and_139 (and_139_out, not_38_out, d_ff_41_q);
  and and_140 (and_140_out, d_ff_40_q, d_ff_36_q);
  and and_141 (and_141_out, not_38_out, d_ff_42_q);
  and and_142 (and_142_out, d_ff_41_q, d_ff_36_q);
  and and_143 (and_143_out, not_38_out, d_ff_43_q);
  and and_144 (and_144_out, d_ff_42_q, d_ff_36_q);
  and and_145 (and_145_out, not_38_out, d_ff_44_q);
  and and_146 (and_146_out, d_ff_43_q, d_ff_36_q);
  and and_147 (and_147_out, not_38_out, d_ff_45_q);
  and and_148 (and_148_out, d_ff_44_q, d_ff_36_q);
  and and_149 (and_149_out, not_38_out, in_9);
  and and_150 (and_150_out, not_39_out, not_40_out);
  or or_64 (or_64_out, and_130_out, and_131_out);
  or or_65 (or_65_out, and_132_out, and_133_out);
  xnor xnor_4 (xnor_4_out, and_124_out, and_125_out);
  or or_66 (or_66_out, and_134_out, and_135_out);
  or or_67 (or_67_out, and_136_out, and_137_out);
  or or_68 (or_68_out, and_138_out, and_139_out);
  or or_69 (or_69_out, and_140_out, and_141_out);
  or or_70 (or_70_out, and_142_out, and_143_out);
  or or_71 (or_71_out, and_144_out, and_145_out);
  or or_72 (or_72_out, and_146_out, and_147_out);
  or or_73 (or_73_out, and_148_out, and_149_out);
  J_K_Flip_Flop #(.trigger("falling")) j_k_ff_23 (
    .J(On_Off_Indicator_5B), .K(On_Off_Indicator_5B), .clk(or_61_out), .Q(j_k_ff_23_q[0]), .Qn(j_k_ff_23_qn),
    .preset(or_60_out), .reset(and_172_out));
  J_K_Flip_Flop #(.trigger("falling")) j_k_ff_24 (
    .J(On_Off_Indicator_5B), .K(On_Off_Indicator_5B), .clk(or_74_out), .Q(j_k_ff_24_q[0]), .Qn(j_k_ff_24_qn),
    .reset(and_173_out));  // open: preset
  or or_74 (or_74_out, and_177_out, and_150_out);
  J_K_Flip_Flop #(.trigger("falling")) j_k_ff_25 (
    .J(or_64_out), .K(or_64_out), .clk(or_56_out), .Q(j_k_ff_19_q[2]), .Qn(j_k_ff_25_qn), .reset(or_75_out));  // open: preset
  or or_75 (or_75_out, and_165_out, and_163_out);
  J_K_Flip_Flop #(.trigger("falling")) j_k_ff_26 (
    .J(or_65_out), .K(or_65_out), .clk(or_57_out), .Q(j_k_ff_20_q[2]), .Qn(j_k_ff_26_qn), .reset(or_76_out));  // open: preset
  or or_76 (or_76_out, and_166_out, and_164_out);
  D_Flip_Flop d_ff_38 (.D(or_66_out), .clk(xnor_4_out), .Q(d_ff_38_q));  // open: Qn, preset, reset
  D_Flip_Flop d_ff_39 (.D(or_67_out), .clk(xnor_4_out), .Q(d_ff_39_q));  // open: Qn, preset, reset
  D_Flip_Flop d_ff_40 (.D(or_68_out), .clk(xnor_4_out), .Q(d_ff_40_q));  // open: Qn, preset, reset
  D_Flip_Flop d_ff_41 (.D(or_69_out), .clk(xnor_4_out), .Q(d_ff_41_q));  // open: Qn, preset, reset
  D_Flip_Flop d_ff_42 (.D(or_70_out), .clk(xnor_4_out), .Q(d_ff_42_q));  // open: Qn, preset, reset
  D_Flip_Flop d_ff_43 (.D(or_71_out), .clk(xnor_4_out), .Q(d_ff_43_q));  // open: Qn, preset, reset
  D_Flip_Flop d_ff_44 (.D(or_72_out), .clk(xnor_4_out), .Q(d_ff_44_q));  // open: Qn, preset, reset
  D_Flip_Flop d_ff_45 (.D(or_73_out), .clk(xnor_4_out), .Q(d_ff_45_q));  // open: Qn, preset, reset
  not not_41 (not_41_out, d_ff_37_q);
  not not_42 (not_42_out, d_ff_37_q);
  and and_151 (and_151_out, and_130_out, j_k_ff_19_q[2]);
  and and_152 (and_152_out, j_k_ff_25_qn, and_131_out);
  and and_153 (and_153_out, and_132_out, j_k_ff_20_q[2]);
  and and_154 (and_154_out, j_k_ff_26_qn, and_133_out);
  and and_155 (and_155_out, d_ff_37_q, j_k_ff_23_q[0]);
  and and_156 (and_156_out, j_k_ff_23_qn, not_41_out);
  and and_157 (and_157_out, d_ff_37_q, j_k_ff_24_q[0]);
  and and_158 (and_158_out, j_k_ff_24_qn, not_42_out);
  or or_77 (or_77_out, and_155_out, and_156_out);
  or or_78 (or_78_out, and_157_out, and_158_out);
  J_K_Flip_Flop #(.trigger("falling")) j_k_ff_27 (
    .J(or_79_out), .K(or_79_out), .clk(or_56_out), .Q(j_k_ff_19_q[3]), .preset(and_176_out),
    .reset(and_163_out));  // open: Qn
  or or_79 (or_79_out, and_151_out, and_152_out);
  J_K_Flip_Flop #(.trigger("falling")) j_k_ff_28 (
    .J(or_80_out), .K(or_80_out), .clk(or_57_out), .Q(j_k_ff_20_q[3]), .reset(and_164_out));  // open: Qn, preset
  or or_80 (or_80_out, and_153_out, and_154_out);
  J_K_Flip_Flop #(.trigger("falling")) j_k_ff_29 (
    .J(or_77_out), .K(or_77_out), .clk(or_61_out), .Q(j_k_ff_23_q[1]), .Qn(j_k_ff_29_qn), .reset(or_81_out));  // open: preset
  or or_81 (or_81_out, and_174_out, and_172_out);
  J_K_Flip_Flop #(.trigger("falling")) j_k_ff_30 (
    .J(or_78_out), .K(or_78_out), .clk(or_74_out), .Q(j_k_ff_24_q[1]), .Qn(j_k_ff_30_qn), .reset(or_82_out));  // open: preset
  or or_82 (or_82_out, and_175_out, and_173_out);
  and and_159 (and_159_out, and_155_out, j_k_ff_23_q[1]);
  and and_160 (and_160_out, j_k_ff_29_qn, and_156_out);
  and and_161 (and_161_out, and_157_out, j_k_ff_24_q[1]);
  and and_162 (and_162_out, j_k_ff_30_qn, and_158_out);
  not not_43 (not_43_out, j_k_ff_19_q[2]);
  not not_44 (not_44_out, j_k_ff_19_q[0]);
  and and_163 (and_163_out, j_k_ff_19_q[3], not_43_out, d_ff_35_q, not_44_out, j_k_ff_19_q[1]);
  and and_164 (and_164_out, j_k_ff_20_q[3], d_ff_35_q, j_k_ff_20_q[1]);
  and and_165 (and_165_out, j_k_ff_19_q[3], j_k_ff_19_q[1], j_k_ff_19_q[0]);
  or or_83 (or_83_out, j_k_ff_20_q[1], j_k_ff_20_q[2]);
  and and_166 (and_166_out, j_k_ff_20_q[3], or_83_out, j_k_ff_20_q[0]);
  J_K_Flip_Flop #(.trigger("falling")) j_k_ff_31 (
    .J(or_84_out), .K(or_84_out), .clk(or_61_out), .Q(j_k_ff_23_q[2]), .Qn(j_k_ff_31_qn), .reset(or_85_out));  // open: preset
  or or_84 (or_84_out, and_159_out, and_160_out);
  or or_85 (or_85_out, and_174_out, and_172_out);
  J_K_Flip_Flop #(.trigger("falling")) j_k_ff_32 (
    .J(or_86_out), .K(or_86_out), .clk(or_74_out), .Q(j_k_ff_24_q[2]), .Qn(j_k_ff_32_qn), .reset(or_87_out));  // open: preset
  or or_86 (or_86_out, and_161_out, and_162_out);
  or or_87 (or_87_out, and_175_out, and_173_out);
  and and_167 (and_167_out, j_k_ff_19_q[0], d_ff_35_q, j_k_ff_19_q[3]);
  or or_88 (or_88_out, j_k_ff_19_q[0], j_k_ff_19_q[1], j_k_ff_19_q[2], j_k_ff_19_q[3]);
  and and_168 (and_168_out, and_159_out, j_k_ff_23_q[2]);
  and and_169 (and_169_out, j_k_ff_31_qn, and_160_out);
  and and_170 (and_170_out, and_161_out, j_k_ff_24_q[2]);
  and and_171 (and_171_out, j_k_ff_32_qn, and_162_out);
  or or_89 (or_89_out, and_168_out, and_169_out);
  or or_90 (or_90_out, and_170_out, and_171_out);
  J_K_Flip_Flop #(.trigger("falling")) j_k_ff_33 (
    .J(or_89_out), .K(or_89_out), .clk(or_61_out), .Q(j_k_ff_23_q[3]), .preset(and_186_out),
    .reset(and_172_out));  // open: Qn
  J_K_Flip_Flop #(.trigger("falling")) j_k_ff_34 (
    .J(or_90_out), .K(or_90_out), .clk(or_74_out), .Q(j_k_ff_24_q[3]), .reset(and_173_out));  // open: Qn, preset
  not not_45 (not_45_out, j_k_ff_23_q[2]);
  not not_46 (not_46_out, j_k_ff_23_q[0]);
  and and_172 (and_172_out, j_k_ff_23_q[3], not_45_out, d_ff_37_q, not_46_out, j_k_ff_23_q[1]);
  and and_173 (and_173_out, j_k_ff_24_q[3], d_ff_37_q, j_k_ff_24_q[1]);
  Hex_Digit_Display hex_digit_display_3 (.value(j_k_ff_20_q));  // open: dp
  Hex_Digit_Display hex_digit_display_4 (.value(j_k_ff_19_q));  // open: dp
  and and_174 (and_174_out, j_k_ff_23_q[3], j_k_ff_23_q[1], j_k_ff_23_q[0]);
  or or_91 (or_91_out, j_k_ff_24_q[1], j_k_ff_24_q[2]);
  and and_175 (and_175_out, j_k_ff_24_q[3], or_91_out, j_k_ff_24_q[0]);
  not not_47 (not_47_out, j_k_ff_19_q[0]);
  not not_48 (not_48_out, j_k_ff_19_q[1]);
  not not_49 (not_49_out, j_k_ff_19_q[2]);
  not not_50 (not_50_out, j_k_ff_19_q[3]);
  and and_176 (and_176_out, not_47_out, not_48_out, not_49_out, not_50_out, not_51_out, not_52_out, not_53_out, not_54_out);
  not not_51 (not_51_out, j_k_ff_20_q[0]);
  not not_52 (not_52_out, j_k_ff_20_q[1]);
  not not_53 (not_53_out, j_k_ff_20_q[2]);
  not not_54 (not_54_out, j_k_ff_20_q[3]);
  and and_177 (and_177_out, j_k_ff_23_q[0], d_ff_37_q, j_k_ff_23_q[3]);
  or or_92 (or_92_out, j_k_ff_23_q[0], j_k_ff_23_q[1], j_k_ff_23_q[2], j_k_ff_23_q[3]);
  and and_178 (and_178_out, On_Off_Indicator_5B, d_ff_38_q);
  and and_179 (and_179_out, On_Off_Indicator_5B, d_ff_39_q);
  and and_180 (and_180_out, On_Off_Indicator_5B, d_ff_40_q);
  LedBar VOLUME_5B (
    .led0(and_178_out), .led1(and_179_out), .led2(and_180_out), .led3(and_181_out), .led4(and_182_out),
    .led5(and_183_out), .led6(and_184_out), .led7(and_185_out));
  and and_181 (and_181_out, On_Off_Indicator_5B, d_ff_41_q);
  and and_182 (and_182_out, On_Off_Indicator_5B, d_ff_42_q);
  Hex_Digit_Display hex_digit_display_5 (.value(j_k_ff_24_q));  // open: dp
  Hex_Digit_Display TRACK_5B (.value(j_k_ff_23_q));  // open: dp
  and and_183 (and_183_out, On_Off_Indicator_5B, d_ff_43_q);
  and and_184 (and_184_out, On_Off_Indicator_5B, d_ff_44_q);
  and and_185 (and_185_out, On_Off_Indicator_5B, d_ff_45_q);
  and and_186 (and_186_out, not_55_out, not_56_out, not_57_out, not_58_out, not_59_out, not_60_out, not_61_out, not_62_out);
  not not_55 (not_55_out, j_k_ff_23_q[0]);
  not not_56 (not_56_out, j_k_ff_23_q[1]);
  not not_57 (not_57_out, j_k_ff_23_q[2]);
  not not_58 (not_58_out, j_k_ff_23_q[3]);
  not not_59 (not_59_out, j_k_ff_24_q[0]);
  not not_60 (not_60_out, j_k_ff_24_q[1]);
  not not_61 (not_61_out, j_k_ff_24_q[2]);
  not not_62 (not_62_out, j_k_ff_24_q[3]);

  // Notes on the sheet:
  //   STAGE 1A
  //   STAGE 1B
  //   STAGE 4
  //   STAGE 5A
  //   Need to press Next_Track_Final for the first time for counting precision
  //   Final Circuit
  //   STAGE 2
  //   Need to press Next_Track_5B for the first time for counting  precision
  //   STAGE 3
  //   STAGE 5A
  //   Need to press Next_Track_5B for the first time for counting  precision
  //   TRACK
endmodule
