// Logisim project Circuit.circ as structural Verilog: 1 circuit, main circuit main
module main (
  input  Play_Button,
  input  Pause_Button
);

  wire and_1_out, and_2_out, d_ff_1_q, d_ff_2_q, d_ff_2_qn;

  D_Flip_Flop d_ff_1 (.D(Play_Button), .clk(Play_Button), .Q(d_ff_1_q));  // open: Qn, preset, reset
  D_Flip_Flop d_ff_2 (
    .D(Play_Button), .clk(Play_Button), .Q(d_ff_2_q), .Qn(d_ff_2_qn), .reset(and_1_out));  // open: preset
  and and_1 (and_1_out, d_ff_1_q, Pause_Button);
  and and_2 (and_2_out, d_ff_2_qn, d_ff_1_q);
  LED Play_LED (.in(d_ff_2_q));
  LED Pause_LED (.in(and_2_out));
endmodule
