// Logisim project Circuit.circ as structural Verilog: 1 circuit, main circuit main
module main (
  input  OnOff_Indicator
);

  wire and_1_out, and_2_out, and_3_out, and_4_out, d_ff_1_q, d_ff_1_qn, Pause_Button_out, Play_Button_out;

  Button Play_Button (.out(Play_Button_out));
  Button Pause_Button (.out(Pause_Button_out));
  and and_1 (and_1_out, OnOff_Indicator, Play_Button_out);
  and and_2 (and_2_out, OnOff_Indicator, Pause_Button_out);
  D_Flip_Flop d_ff_1 (
    .D(OnOff_Indicator), .clk(and_1_out), .Q(d_ff_1_q), .Qn(d_ff_1_qn), .reset(and_2_out));  // open: preset
  and and_3 (and_3_out, OnOff_Indicator, d_ff_1_q);
  and and_4 (and_4_out, d_ff_1_qn, OnOff_Indicator);
  LED Play_LED (.in(and_3_out));
  LED Pause_LED (.in(and_4_out));
endmodule
