// Logisim project CircuitFinal.circ as structural Verilog: 1 circuit, main circuit main
module main (
);

  wire and_1_out, and_2_out, d_ff_1_q, d_ff_2_q, d_ff_2_qn, d_ff_3_q, Pause_Button_out, Play_Button_out;

  Button Play_Button (.out(Play_Button_out));
  Button Pause_Button (.out(Pause_Button_out));
  D_Flip_Flop d_ff_1 (.D(Play_Button_out), .clk(Play_Button_out), .Q(d_ff_1_q));  // open: Qn, preset, reset
  D_Flip_Flop d_ff_2 (
    .D(Play_Button_out), .clk(Play_Button_out), .Q(d_ff_2_q), .Qn(d_ff_2_qn), .preset(d_ff_3_q),
    .reset(and_1_out));
  and and_1 (and_1_out, d_ff_1_q, Pause_Button_out);
  and and_2 (and_2_out, d_ff_2_qn, d_ff_1_q);
  D_Flip_Flop d_ff_3 (.D(and_2_out), .clk(Pause_Button_out), .Q(d_ff_3_q));  // open: Qn, preset, reset
  LED Play_LED (.in(d_ff_2_q));
  LED Pause_LED (.in(and_2_out));
endmodule
