// Logisim project Circuit.circ as structural Verilog: 1 circuit, main circuit main
module main (
  input  On_Off_Indicator,
  input  in_2,
  input  in_3
);

  wire and_1_out, and_2_out, and_3_out, and_4_out, and_5_out, and_6_out, and_7_out, and_8_out, and_9_out,
       and_10_out, and_11_out, and_12_out, and_13_out, and_14_out, and_15_out, and_16_out, and_17_out,
       and_18_out, and_19_out, and_20_out, and_21_out, and_22_out, and_23_out, and_24_out, d_ff_1_q,
       d_ff_2_q, d_ff_3_q, d_ff_4_q, d_ff_5_q, d_ff_6_q, d_ff_7_q, d_ff_8_q, d_ff_9_q, not_1_out, or_1_out,
       or_2_out, or_3_out, or_4_out, or_5_out, or_6_out, or_7_out, or_8_out, Volume_Down_out, Volume_Up_out,
       xnor_1_out;

  Button Volume_Up (.out(Volume_Up_out));
  Button Volume_Down (.out(Volume_Down_out));
  D_Flip_Flop d_ff_1 (.Q(d_ff_1_q), .preset(Volume_Up_out), .reset(Volume_Down_out));  // open: D, clk, Qn
  not not_1 (not_1_out, d_ff_1_q);
  and and_1 (and_1_out, in_3, d_ff_1_q);
  and and_2 (and_2_out, not_1_out, d_ff_3_q);
  and and_3 (and_3_out, d_ff_2_q, d_ff_1_q);
  and and_4 (and_4_out, not_1_out, d_ff_4_q);
  and and_5 (and_5_out, d_ff_3_q, d_ff_1_q);
  and and_6 (and_6_out, not_1_out, d_ff_5_q);
  and and_7 (and_7_out, d_ff_4_q, d_ff_1_q);
  and and_8 (and_8_out, not_1_out, d_ff_6_q);
  and and_9 (and_9_out, d_ff_5_q, d_ff_1_q);
  and and_10 (and_10_out, not_1_out, d_ff_7_q);
  and and_11 (and_11_out, d_ff_6_q, d_ff_1_q);
  and and_12 (and_12_out, not_1_out, d_ff_8_q);
  and and_13 (and_13_out, d_ff_7_q, d_ff_1_q);
  and and_14 (and_14_out, not_1_out, d_ff_9_q);
  and and_15 (and_15_out, d_ff_8_q, d_ff_1_q);
  and and_16 (and_16_out, not_1_out, in_2);
  xnor xnor_1 (xnor_1_out, Volume_Up_out, Volume_Down_out);
  or or_1 (or_1_out, and_1_out, and_2_out);
  or or_2 (or_2_out, and_3_out, and_4_out);
  or or_3 (or_3_out, and_5_out, and_6_out);
  or or_4 (or_4_out, and_7_out, and_8_out);
  or or_5 (or_5_out, and_9_out, and_10_out);
  or or_6 (or_6_out, and_11_out, and_12_out);
  or or_7 (or_7_out, and_13_out, and_14_out);
  or or_8 (or_8_out, and_15_out, and_16_out);
  D_Flip_Flop d_ff_2 (.D(or_1_out), .clk(xnor_1_out), .Q(d_ff_2_q));  // open: Qn, preset, reset
  D_Flip_Flop d_ff_3 (.D(or_2_out), .clk(xnor_1_out), .Q(d_ff_3_q));  // open: Qn, preset, reset
  D_Flip_Flop d_ff_4 (.D(or_3_out), .clk(xnor_1_out), .Q(d_ff_4_q));  // open: Qn, preset, reset
  D_Flip_Flop d_ff_5 (.D(or_4_out), .clk(xnor_1_out), .Q(d_ff_5_q));  // open: Qn, preset, reset
  D_Flip_Flop d_ff_6 (.D(or_5_out), .clk(xnor_1_out), .Q(d_ff_6_q));  // open: Qn, preset, reset
  D_Flip_Flop d_ff_7 (.D(or_6_out), .clk(xnor_1_out), .Q(d_ff_7_q));  // open: Qn, preset, reset
  D_Flip_Flop d_ff_8 (.D(or_7_out), .clk(xnor_1_out), .Q(d_ff_8_q));  // open: Qn, preset, reset
  D_Flip_Flop d_ff_9 (.D(or_8_out), .clk(xnor_1_out), .Q(d_ff_9_q));  // open: Qn, preset, reset
  and and_17 (and_17_out, d_ff_2_q, On_Off_Indicator);
  LedBar ledbar_1 (
    .led0(and_17_out), .led1(and_18_out), .led2(and_19_out), .led3(and_20_out), .led4(and_21_out),
    .led5(and_22_out), .led6(and_23_out), .led7(and_24_out));
  and and_18 (and_18_out, d_ff_3_q, On_Off_Indicator);
  and and_19 (and_19_out, d_ff_4_q, On_Off_Indicator);
  and and_20 (and_20_out, d_ff_5_q, On_Off_Indicator);
  and and_21 (and_21_out, d_ff_6_q, On_Off_Indicator);
  and and_22 (and_22_out, d_ff_7_q, On_Off_Indicator);
  and and_23 (and_23_out, d_ff_8_q, On_Off_Indicator);
  and and_24 (and_24_out, d_ff_9_q, On_Off_Indicator);
endmodule
