// Logisim project sketchIDEA.circ as structural Verilog: 1 circuit, main circuit main
module main (
  input  left_TO_right,
  input  DATA,
  input  On_Off,
  input  in_4
);

  wire and_1_out, and_2_out, and_3_out, and_4_out, and_5_out, and_6_out, and_7_out, and_8_out, and_9_out,
       and_10_out, and_11_out, and_12_out, button_1_out, CLK_out, d_ff_1_q, d_ff_2_q, d_ff_3_q, d_ff_4_q,
       d_ff_5_q, d_ff_6_q, d_ff_7_q, d_ff_8_q, d_ff_9_q, nand_1_out, nand_2_out, nand_3_out, nand_4_out,
       nand_5_out, nand_6_out, nand_7_out, nand_8_out, nand_9_out, nand_10_out, nand_11_out, nand_12_out,
       not_1_out, not_2_out, not_3_out, Off_Button_out, On_Button_out, or_1_out, or_2_out, or_3_out,
       or_4_out, RESET_out, xnor_1_out;

  Button On_Button (.out(On_Button_out));
  Button Off_Button (.out(Off_Button_out));
  nand nand_1 (nand_1_out, d_ff_3_q, not_3_out);
  nand nand_2 (nand_2_out, left_TO_right, DATA);
  D_Flip_Flop d_ff_1 (.Q(d_ff_1_q), .preset(On_Button_out), .reset(Off_Button_out));  // open: D, clk, Qn
  nand nand_3 (nand_3_out, nand_1_out, nand_2_out);
  D_Flip_Flop d_ff_2 (.D(nand_3_out), .clk(CLK_out), .Q(d_ff_2_q), .reset(RESET_out));  // open: Qn, preset
  Button RESET (.out(RESET_out));
  Button CLK (.out(CLK_out));
  not not_1 (not_1_out, d_ff_1_q);
  not not_2 (not_2_out, not_1_out);
  nand nand_4 (nand_4_out, d_ff_8_q, not_3_out);
  nand nand_5 (nand_5_out, nand_4_out, nand_6_out);
  nand nand_6 (nand_6_out, left_TO_right, d_ff_2_q);
  and and_1 (and_1_out, On_Off, not_2_out);
  or or_1 (or_1_out, and_1_out, and_2_out);
  and and_2 (and_2_out, not_1_out, d_ff_5_q);
  and and_3 (and_3_out, d_ff_4_q, not_2_out);
  or or_2 (or_2_out, and_3_out, and_4_out);
  and and_4 (and_4_out, not_1_out, d_ff_6_q);
  and and_5 (and_5_out, d_ff_5_q, not_2_out);
  or or_3 (or_3_out, and_5_out, and_6_out);
  and and_6 (and_6_out, not_1_out, d_ff_7_q);
  and and_7 (and_7_out, d_ff_6_q, not_2_out);
  or or_4 (or_4_out, and_7_out, and_8_out);
  and and_8 (and_8_out, in_4, not_1_out);
  D_Flip_Flop d_ff_3 (.D(nand_5_out), .clk(CLK_out), .Q(d_ff_3_q), .reset(RESET_out));  // open: Qn, preset
  xnor xnor_1 (xnor_1_out, On_Button_out, Off_Button_out);
  nand nand_7 (nand_7_out, d_ff_9_q, not_3_out);
  nand nand_8 (nand_8_out, left_TO_right, d_ff_3_q);
  D_Flip_Flop d_ff_4 (.D(or_1_out), .clk(xnor_1_out), .Q(d_ff_4_q), .reset(button_1_out));  // open: Qn, preset
  D_Flip_Flop d_ff_5 (.D(or_2_out), .clk(xnor_1_out), .Q(d_ff_5_q), .reset(button_1_out));  // open: Qn, preset
  D_Flip_Flop d_ff_6 (.D(or_3_out), .clk(xnor_1_out), .Q(d_ff_6_q), .reset(button_1_out));  // open: Qn, preset
  D_Flip_Flop d_ff_7 (.D(or_4_out), .clk(xnor_1_out), .Q(d_ff_7_q), .reset(button_1_out));  // open: Qn, preset
  nand nand_9 (nand_9_out, nand_7_out, nand_8_out);
  D_Flip_Flop d_ff_8 (.D(nand_9_out), .clk(CLK_out), .Q(d_ff_8_q), .reset(RESET_out));  // open: Qn, preset
  not not_3 (not_3_out, left_TO_right);
  nand nand_10 (nand_10_out, DATA, not_3_out);
  nand nand_11 (nand_11_out, nand_10_out, nand_12_out);
  nand nand_12 (nand_12_out, left_TO_right, d_ff_8_q);
  D_Flip_Flop d_ff_9 (.D(nand_11_out), .clk(CLK_out), .Q(d_ff_9_q), .reset(RESET_out));  // open: Qn, preset
  and and_9 (and_9_out, On_Off, d_ff_4_q);
  and and_10 (and_10_out, On_Off, d_ff_5_q);
  LED led_1 (.in(and_9_out));
  LED led_2 (.in(and_10_out));
  and and_11 (and_11_out, On_Off, d_ff_6_q);
  and and_12 (and_12_out, On_Off, d_ff_7_q);
  LED led_3 (.in(and_11_out));
  LED led_4 (.in(and_12_out));
  Button button_1 (.out(button_1_out));

  // Notes on the sheet:
  //   First Implementation
endmodule
