// Logisim project Circuit.circ as structural Verilog: 1 circuit, main circuit main
module main (
  input  in_1
);

  wire and_1_out, and_2_out, and_3_out, and_4_out, and_5_out, and_6_out, and_7_out, and_8_out, and_9_out,
       and_10_out, and_11_out, and_12_out, and_13_out, and_14_out, and_15_out, and_16_out, and_17_out,
       and_18_out, and_19_out, d_ff_1_q, j_k_ff_1_qn, j_k_ff_2_qn, j_k_ff_3_qn, j_k_ff_4_qn, j_k_ff_5_qn,
       j_k_ff_6_qn, Next_Track_out, not_1_out, not_2_out, not_3_out, not_4_out, not_5_out, not_6_out,
       not_7_out, not_8_out, not_9_out, not_10_out, not_11_out, not_12_out, not_13_out, not_14_out, or_1_out,
       or_2_out, or_3_out, or_4_out, or_5_out, or_6_out, or_7_out, or_8_out, or_9_out, or_10_out, or_11_out,
       or_12_out, or_13_out, or_14_out, or_15_out, Previous_Track_out;
  wire [3:0] j_k_ff_1_q, j_k_ff_2_q;

  Button Next_Track (.out(Next_Track_out));
  Button Previous_Track (.out(Previous_Track_out));
  or or_1 (or_1_out, and_15_out, and_19_out);
  D_Flip_Flop d_ff_1 (.Q(d_ff_1_q), .preset(Next_Track_out), .reset(Previous_Track_out));  // open: D, clk, Qn
  or or_2 (or_2_out, Next_Track_out, Previous_Track_out);
  not not_1 (not_1_out, or_15_out);
  not not_2 (not_2_out, d_ff_1_q);
  and and_1 (and_1_out, not_1_out, not_2_out);
  or or_3 (or_3_out, and_18_out, and_1_out);
  J_K_Flip_Flop #(.trigger("falling")) j_k_ff_1 (
    .J(in_1), .K(in_1), .clk(or_2_out), .Q(j_k_ff_1_q[0]), .Qn(j_k_ff_1_qn), .preset(or_1_out),
    .reset(and_14_out));
  J_K_Flip_Flop #(.trigger("falling")) j_k_ff_2 (
    .J(in_1), .K(in_1), .clk(or_3_out), .Q(j_k_ff_2_q[0]), .Qn(j_k_ff_2_qn), .reset(and_15_out));  // open: preset
  not not_3 (not_3_out, d_ff_1_q);
  not not_4 (not_4_out, d_ff_1_q);
  and and_2 (and_2_out, d_ff_1_q, j_k_ff_1_q[0]);
  and and_3 (and_3_out, j_k_ff_1_qn, not_3_out);
  and and_4 (and_4_out, d_ff_1_q, j_k_ff_2_q[0]);
  and and_5 (and_5_out, j_k_ff_2_qn, not_4_out);
  J_K_Flip_Flop #(.trigger("falling")) j_k_ff_3 (
    .J(or_4_out), .K(or_4_out), .clk(or_2_out), .Q(j_k_ff_1_q[1]), .Qn(j_k_ff_3_qn), .reset(or_6_out));  // open: preset
  or or_4 (or_4_out, and_2_out, and_3_out);
  J_K_Flip_Flop #(.trigger("falling")) j_k_ff_4 (
    .J(or_5_out), .K(or_5_out), .clk(or_3_out), .Q(j_k_ff_2_q[1]), .Qn(j_k_ff_4_qn), .reset(or_7_out));  // open: preset
  or or_5 (or_5_out, and_4_out, and_5_out);
  or or_6 (or_6_out, and_16_out, and_14_out);
  or or_7 (or_7_out, and_17_out, and_15_out);
  and and_6 (and_6_out, and_2_out, j_k_ff_1_q[1]);
  and and_7 (and_7_out, j_k_ff_3_qn, and_3_out);
  and and_8 (and_8_out, and_4_out, j_k_ff_2_q[1]);
  and and_9 (and_9_out, j_k_ff_4_qn, and_5_out);
  or or_8 (or_8_out, and_6_out, and_7_out);
  or or_9 (or_9_out, and_8_out, and_9_out);
  J_K_Flip_Flop #(.trigger("falling")) j_k_ff_5 (
    .J(or_8_out), .K(or_8_out), .clk(or_2_out), .Q(j_k_ff_1_q[2]), .Qn(j_k_ff_5_qn), .reset(or_10_out));  // open: preset
  or or_10 (or_10_out, and_16_out, and_14_out);
  J_K_Flip_Flop #(.trigger("falling")) j_k_ff_6 (
    .J(or_9_out), .K(or_9_out), .clk(or_3_out), .Q(j_k_ff_2_q[2]), .Qn(j_k_ff_6_qn), .reset(or_11_out));  // open: preset
  or or_11 (or_11_out, and_17_out, and_15_out);
  and and_10 (and_10_out, and_6_out, j_k_ff_1_q[2]);
  and and_11 (and_11_out, j_k_ff_5_qn, and_7_out);
  and and_12 (and_12_out, and_8_out, j_k_ff_2_q[2]);
  and and_13 (and_13_out, j_k_ff_6_qn, and_9_out);
  J_K_Flip_Flop #(.trigger("falling")) j_k_ff_7 (
    .J(or_12_out), .K(or_12_out), .clk(or_2_out), .Q(j_k_ff_1_q[3]), .preset(and_19_out), .reset(and_14_out));  // open: Qn
  or or_12 (or_12_out, and_10_out, and_11_out);
  J_K_Flip_Flop #(.trigger("falling")) j_k_ff_8 (
    .J(or_13_out), .K(or_13_out), .clk(or_3_out), .Q(j_k_ff_2_q[3]), .reset(and_15_out));  // open: Qn, preset
  or or_13 (or_13_out, and_12_out, and_13_out);
  not not_5 (not_5_out, j_k_ff_1_q[2]);
  not not_6 (not_6_out, j_k_ff_1_q[0]);
  and and_14 (and_14_out, j_k_ff_1_q[3], not_5_out, d_ff_1_q, not_6_out, j_k_ff_1_q[1]);
  and and_15 (and_15_out, j_k_ff_2_q[3], d_ff_1_q, j_k_ff_2_q[1]);
  and and_16 (and_16_out, j_k_ff_1_q[3], j_k_ff_1_q[1], j_k_ff_1_q[0]);
  or or_14 (or_14_out, j_k_ff_2_q[1], j_k_ff_2_q[2]);
  and and_17 (and_17_out, j_k_ff_2_q[3], or_14_out, j_k_ff_2_q[0]);
  and and_18 (and_18_out, j_k_ff_1_q[0], d_ff_1_q, j_k_ff_1_q[3]);
  or or_15 (or_15_out, j_k_ff_1_q[0], j_k_ff_1_q[1], j_k_ff_1_q[2], j_k_ff_1_q[3]);
  Hex_Digit_Display hex_digit_display_1 (.value(j_k_ff_2_q));  // open: dp
  Hex_Digit_Display hex_digit_display_2 (.value(j_k_ff_1_q));  // open: dp
  not not_7 (not_7_out, j_k_ff_1_q[0]);
  not not_8 (not_8_out, j_k_ff_1_q[1]);
  not not_9 (not_9_out, j_k_ff_1_q[2]);
  not not_10 (not_10_out, j_k_ff_1_q[3]);
  and and_19 (and_19_out, not_7_out, not_8_out, not_9_out, not_10_out, not_11_out, not_12_out, not_13_out, not_14_out);
  not not_11 (not_11_out, j_k_ff_2_q[0]);
  not not_12 (not_12_out, j_k_ff_2_q[1]);
  not not_13 (not_13_out, j_k_ff_2_q[2]);
  not not_14 (not_14_out, j_k_ff_2_q[3]);

  // Notes on the sheet:
  //   TRACK
endmodule
