// Logisim project draft.circ as structural Verilog: 1 circuit, main circuit main
module main (
  input  in_1,
  input  in_2,
  input  in_3,
  input  On_Off_Indicator,
  input  in_5
);

  wire and_1_out, and_2_out, and_3_out, and_4_out, and_5_out, and_7_out, and_8_out, and_9_out, and_12_out,
       and_13_out, and_14_out, and_16_out, and_17_out, and_18_out, and_21_out, and_22_out, and_24_out,
       and_26_out, and_27_out, button_1_out, button_3_out, button_4_out, button_5_out, button_6_out,
       button_7_out, Clock_out, d_ff_1_q, j_k_ff_3_qn, j_k_ff_6_qn, j_k_ff_7_qn, j_k_ff_8_qn, j_k_ff_9_qn,
       j_k_ff_12_qn, j_k_ff_13_qn, j_k_ff_15_qn, j_k_ff_17_qn, j_k_ff_19_qn, j_k_ff_20_qn, j_k_ff_21_qn,
       LowerThan0Set9_out, Next_Track_out, nor_1_out, nor_2_out, nor_4_out, not_1_out, not_2_out, not_3_out,
       not_4_out, not_5_out, not_6_out, not_7_out, not_8_out, not_9_out, or_1_out, or_2_out, or_4_out,
       or_5_out, or_6_out, or_7_out, or_8_out, or_9_out, or_11_out, or_12_out, or_13_out, Previous_Track_out,
       Reset0WhenReaching10_out, undriven;
  wire [3:0] j_k_ff_1_q, j_k_ff_3_q, j_k_ff_8_q, j_k_ff_10_q;
  wire [3:3] button_2_out;

  Button button_1 (.out(button_1_out));
  J_K_Flip_Flop j_k_ff_1 (
    .J(in_2), .K(in_2), .clk(button_1_out), .Q(j_k_ff_1_q[0]), .reset(and_4_out));  // open: Qn, preset
  Button button_2 (.out(button_2_out[3]));
  Button Next_Track (.out(Next_Track_out));
  Button Previous_Track (.out(Previous_Track_out));
  J_K_Flip_Flop j_k_ff_2 (
    .J(j_k_ff_1_q[0]), .K(j_k_ff_1_q[0]), .clk(button_1_out), .Q(j_k_ff_1_q[1]), .reset(and_4_out));  // open: Qn, preset
  Button button_3 (.out(button_3_out));
  Button button_4 (.out(button_4_out));
  J_K_Flip_Flop j_k_ff_3 (
    .J(in_3), .K(in_3), .clk(button_2_out[3]), .Q(j_k_ff_3_q[0]), .Qn(j_k_ff_3_qn), .reset(button_7_out));  // open: preset
  D_Flip_Flop d_ff_1 (.Q(d_ff_1_q), .preset(button_3_out), .reset(button_4_out));  // open: D, clk, Qn
  and and_1 (and_1_out, j_k_ff_1_q[0], j_k_ff_1_q[1]);
  J_K_Flip_Flop j_k_ff_4 (
    .J(and_1_out), .K(and_1_out), .clk(button_1_out), .Q(j_k_ff_1_q[2]), .reset(and_4_out));  // open: Qn, preset
  Button button_5 (.out(button_5_out));
  Button button_6 (.out(button_6_out));
  nor nor_1 (nor_1_out, Next_Track_out, nor_2_out);
  nor nor_2 (nor_2_out, nor_1_out, Previous_Track_out);
  or or_1 (or_1_out, button_3_out, button_4_out);
  J_K_Flip_Flop j_k_ff_5 (
    .J(and_2_out), .K(and_2_out), .clk(button_1_out), .Q(j_k_ff_1_q[3]), .reset(and_4_out));  // open: Qn, preset
  J_K_Flip_Flop j_k_ff_6 (
    .J(j_k_ff_3_qn), .K(j_k_ff_3_qn), .clk(button_2_out[3]), .Q(j_k_ff_3_q[1]), .Qn(j_k_ff_6_qn),
    .reset(button_7_out));  // open: preset
  or Clock (Clock_out, Next_Track_out, Previous_Track_out);
  and and_2 (and_2_out, j_k_ff_1_q[2], and_1_out);
  and and_3 (and_3_out, j_k_ff_6_qn, j_k_ff_3_qn);
  and and_4 (and_4_out, j_k_ff_1_q[1], j_k_ff_1_q[3]);
  J_K_Flip_Flop j_k_ff_7 (
    .J(and_3_out), .K(and_3_out), .clk(button_2_out[3]), .Q(j_k_ff_3_q[2]), .Qn(j_k_ff_7_qn),
    .reset(button_7_out));  // open: preset
  nor nor_3 (On_Off_Indicator, button_5_out, nor_4_out);
  nor nor_4 (nor_4_out, On_Off_Indicator, button_6_out);
  or or_2 (or_2_out, button_5_out, button_6_out);
  not not_1 (not_1_out, nor_2_out);
  J_K_Flip_Flop #(.trigger("falling")) j_k_ff_8 (
    .J(in_5), .K(in_5), .clk(or_1_out), .Q(j_k_ff_8_q[0]), .Qn(j_k_ff_8_qn), .reset(Reset0WhenReaching10_out));  // open: preset
  and and_5 (and_5_out, j_k_ff_7_qn, and_3_out);
  or or_3 (button_2_out[3], nor_1_out, button_2_out[3]);
  J_K_Flip_Flop #(.trigger("falling")) j_k_ff_9 (
    .J(On_Off_Indicator), .K(On_Off_Indicator), .clk(Clock_out), .Q(button_2_out[3]), .Qn(j_k_ff_9_qn),
    .preset(or_2_out), .reset(and_27_out));
  not not_2 (not_2_out, d_ff_1_q);
  J_K_Flip_Flop j_k_ff_10 (
    .J(in_1), .K(in_1), .clk(and_4_out), .Q(j_k_ff_10_q[0]), .reset(and_18_out));  // open: Qn, preset
  J_K_Flip_Flop j_k_ff_11 (
    .J(and_5_out), .K(and_5_out), .clk(button_2_out[3]), .Q(j_k_ff_3_q[3]), .reset(button_7_out));  // open: Qn, preset
  and and_6 (or_2_out, nor_2_out, button_2_out[3]);
  and and_7 (and_7_out, j_k_ff_9_qn, not_1_out);
  and and_8 (and_8_out, d_ff_1_q, j_k_ff_8_q[0]);
  and and_9 (and_9_out, j_k_ff_8_qn, not_2_out);
  Hex_Digit_Display hex_digit_display_1 (.value(j_k_ff_10_q));  // open: dp
  Hex_Digit_Display hex_digit_display_2 (.value(j_k_ff_1_q));  // open: dp
  Button button_7 (.out(button_7_out));
  J_K_Flip_Flop #(.trigger("falling")) j_k_ff_12 (
    .J(undriven), .K(undriven), .clk(or_2_out), .Q(button_2_out[3]), .Qn(j_k_ff_12_qn),
    .preset(button_2_out[3]), .reset(or_2_out));
  not not_3 (not_3_out, nor_4_out);
  J_K_Flip_Flop #(.trigger("falling")) j_k_ff_13 (
    .J(or_4_out), .K(or_4_out), .clk(or_1_out), .Q(j_k_ff_8_q[1]), .Qn(j_k_ff_13_qn),
    .reset(Reset0WhenReaching10_out));  // open: preset
  or or_4 (or_4_out, and_8_out, and_9_out);
  J_K_Flip_Flop j_k_ff_14 (
    .J(j_k_ff_10_q[0]), .K(j_k_ff_10_q[0]), .clk(and_4_out), .Q(j_k_ff_10_q[1]), .reset(and_18_out));  // open: Qn, preset
  and and_10 (button_2_out[3], nor_4_out, button_2_out[3]);
  and and_11 (or_2_out, j_k_ff_12_qn, not_3_out);
  J_K_Flip_Flop #(.trigger("falling")) j_k_ff_15 (
    .J(or_5_out), .K(or_5_out), .clk(Clock_out), .Q(button_2_out[3]), .Qn(j_k_ff_15_qn), .preset(or_2_out),
    .reset(and_27_out));
  or or_5 (or_5_out, or_2_out, and_7_out);
  and and_12 (and_12_out, j_k_ff_10_q[0], j_k_ff_10_q[1]);
  J_K_Flip_Flop j_k_ff_16 (
    .J(and_12_out), .K(and_12_out), .clk(and_4_out), .Q(j_k_ff_10_q[2]), .reset(and_18_out));  // open: Qn, preset
  Hex_Digit_Display hex_digit_display_3 (.value(j_k_ff_3_q));  // open: dp
  and and_13 (and_13_out, and_8_out, j_k_ff_8_q[1]);
  and and_14 (and_14_out, j_k_ff_13_qn, and_9_out);
  J_K_Flip_Flop #(.trigger("falling")) j_k_ff_17 (
    .J(or_6_out), .K(or_6_out), .clk(or_2_out), .Q(button_2_out[3]), .Qn(j_k_ff_17_qn),
    .preset(button_2_out[3]), .reset(or_7_out));
  or or_6 (or_6_out, button_2_out[3], or_2_out);
  or or_7 (or_7_out, button_2_out[3], or_2_out);
  and and_15 (or_2_out, or_2_out, button_2_out[3]);
  and and_16 (and_16_out, j_k_ff_15_qn, and_7_out);
  or or_8 (or_8_out, and_13_out, and_14_out);
  and and_17 (and_17_out, j_k_ff_10_q[2], and_12_out);
  J_K_Flip_Flop j_k_ff_18 (
    .J(and_17_out), .K(and_17_out), .clk(and_4_out), .Q(j_k_ff_10_q[3]), .reset(and_18_out));  // open: Qn, preset
  or or_9 (or_9_out, or_2_out, and_16_out);
  J_K_Flip_Flop #(.trigger("falling")) j_k_ff_19 (
    .J(or_8_out), .K(or_8_out), .clk(or_1_out), .Q(j_k_ff_8_q[2]), .Qn(j_k_ff_19_qn),
    .reset(Reset0WhenReaching10_out));  // open: preset
  and and_18 (and_18_out, j_k_ff_10_q[1], j_k_ff_10_q[3]);
  and and_19 (button_2_out[3], button_2_out[3], button_2_out[3]);
  and and_20 (or_2_out, j_k_ff_17_qn, or_2_out);
  J_K_Flip_Flop j_k_ff_20 (
    .J(or_9_out), .K(or_9_out), .clk(Clock_out), .Q(button_2_out[3]), .Qn(j_k_ff_20_qn), .preset(or_2_out),
    .reset(and_27_out));
  and and_21 (and_21_out, and_13_out, j_k_ff_8_q[2]);
  and and_22 (and_22_out, j_k_ff_19_qn, and_14_out);
  J_K_Flip_Flop #(.trigger("falling")) j_k_ff_21 (
    .J(button_2_out[3]), .K(button_2_out[3]), .clk(or_2_out), .Q(button_2_out[3]), .Qn(j_k_ff_21_qn),
    .preset(button_2_out[3]), .reset(or_11_out));
  or or_10 (button_2_out[3], button_2_out[3], or_2_out);
  or or_11 (or_11_out, button_2_out[3], or_2_out);
  and and_23 (or_2_out, or_2_out, button_2_out[3]);
  and and_24 (and_24_out, j_k_ff_20_qn, and_16_out);
  J_K_Flip_Flop j_k_ff_22 (
    .J(or_12_out), .K(or_12_out), .clk(or_1_out), .Q(j_k_ff_8_q[3]), .reset(Reset0WhenReaching10_out));  // open: Qn, preset
  or or_12 (or_12_out, and_21_out, and_22_out);
  and and_25 (button_2_out[3], button_2_out[3], button_2_out[3]);
  and and_26 (and_26_out, j_k_ff_21_qn, or_2_out);
  or or_13 (or_13_out, or_2_out, and_24_out);
  or or_14 (button_2_out[3], button_2_out[3], and_26_out);
  J_K_Flip_Flop j_k_ff_23 (
    .J(or_13_out), .K(or_13_out), .clk(Clock_out), .Q(button_2_out[3]), .preset(or_2_out), .reset(and_27_out));  // open: Qn
  Hex_Digit_Display hex_digit_display_4 (.value(j_k_ff_8_q));  // open: dp
  J_K_Flip_Flop #(.trigger("falling")) j_k_ff_24 (
    .J(button_2_out[3]), .K(button_2_out[3]), .clk(or_2_out), .Q(button_2_out[3]), .preset(button_2_out[3]),
    .reset(or_2_out));  // open: Qn
  and Reset0WhenReaching10 (Reset0WhenReaching10_out, j_k_ff_8_q[3], j_k_ff_8_q[1]);
  and NoGreaterThan9 (or_2_out, button_2_out[3], nor_4_out, button_2_out[3]);
  not not_4 (not_4_out, button_2_out[3]);
  not not_5 (not_5_out, button_2_out[3]);
  and and_27 (and_27_out, button_2_out[3], not_4_out, not_5_out, button_2_out[3]);
  // Hex_Digit_Display hex_digit_display_5: pin names not known; wires that end beside it: {4{button_2_out[3]}}
  and NoLowerThan0 (button_2_out[3], button_2_out[3], button_2_out[3], button_2_out[3]);
  not not_6 (not_6_out, j_k_ff_8_q[3]);
  not not_7 (not_7_out, j_k_ff_8_q[2]);
  not not_8 (not_8_out, j_k_ff_8_q[1]);
  not not_9 (not_9_out, j_k_ff_8_q[0]);
  and LowerThan0Set9 (LowerThan0Set9_out, not_6_out, not_7_out, not_8_out, not_9_out);
  // OR_Gate LowerThan9NoChange has open pins: in0=button_2_out[3], in1=button_2_out[3], in2=button_2_out[3], in3=button_2_out[3], out=open

  // Notes on the sheet:
  //   Implementation of track skipping
  //   Synchronous Circuit Counting Down
endmodule
