// Logisim project Circuit.circ as structural Verilog: 1 circuit, main circuit main
module main (
  input  On_Off_Indicator,
  input  On_Off_Indicator_Final,
  input  in_3
);

  wire and_1_out, and_2_out, and_3_out, and_4_out, and_5_out, and_6_out, and_7_out, and_8_out, and_9_out,
       and_10_out, and_11_out, and_12_out, and_13_out, and_14_out, and_15_out, and_16_out, and_17_out,
       and_18_out, and_19_out, and_20_out, and_21_out, and_22_out, and_23_out, and_24_out, and_25_out,
       and_26_out, and_27_out, and_28_out, and_29_out, and_30_out, and_31_out, and_32_out, and_33_out,
       and_34_out, and_35_out, and_36_out, and_37_out, and_38_out, and_39_out, and_40_out, and_41_out,
       and_42_out, and_43_out, and_44_out, and_45_out, and_46_out, and_47_out, and_48_out, and_49_out,
       d_ff_1_q, d_ff_2_q, d_ff_3_q, d_ff_4_q, d_ff_5_q, d_ff_6_q, d_ff_7_q, d_ff_8_q, d_ff_9_q, d_ff_10_q,
       j_k_ff_1_q, j_k_ff_1_qn, j_k_ff_2_q, j_k_ff_2_qn, j_k_ff_3_qn, j_k_ff_4_qn, j_k_ff_5_qn, j_k_ff_6_qn,
       j_k_ff_7_qn, j_k_ff_8_qn, Next_Track_Final_out, not_1_out, not_2_out, not_3_out, not_4_out, not_5_out,
       not_6_out, not_7_out, not_8_out, not_9_out, not_10_out, not_11_out, not_12_out, not_13_out,
       not_14_out, not_15_out, not_16_out, not_17_out, or_1_out, or_2_out, or_3_out, or_4_out, or_5_out,
       or_6_out, or_7_out, or_8_out, or_9_out, or_10_out, or_11_out, or_12_out, or_13_out, or_14_out,
       or_15_out, or_16_out, or_17_out, or_18_out, or_19_out, or_20_out, or_21_out, or_22_out, or_23_out,
       Play_Pause_Button_Final_out, Play_Pause_Button_out, Previous_Track_Final_out, Volume_Down_Final_out,
       Volume_Up_Final_out, xnor_1_out;
  wire [3:0] j_k_ff_3_q, j_k_ff_4_q;

  Button Play_Pause_Button (.out(Play_Pause_Button_out));
  J_K_Flip_Flop j_k_ff_1 (
    .J(On_Off_Indicator), .K(Play_Pause_Button_out), .clk(Play_Pause_Button_out), .Q(j_k_ff_1_q),
    .Qn(j_k_ff_1_qn), .reset(not_1_out));  // open: preset
  not not_1 (not_1_out, On_Off_Indicator);
  and and_1 (and_1_out, On_Off_Indicator, j_k_ff_1_q);
  and and_2 (and_2_out, j_k_ff_1_qn, On_Off_Indicator);
  Button Play_Pause_Button_Final (.out(Play_Pause_Button_Final_out));
  Button Volume_Up_Final (.out(Volume_Up_Final_out));
  Button Volume_Down_Final (.out(Volume_Down_Final_out));
  Button Next_Track_Final (.out(Next_Track_Final_out));
  Button Previous_Track_Final (.out(Previous_Track_Final_out));
  LED Play_LED (.in(and_1_out));
  LED Pause_LED (.in(and_2_out));
  J_K_Flip_Flop j_k_ff_2 (
    .J(On_Off_Indicator_Final), .K(Play_Pause_Button_Final_out), .clk(Play_Pause_Button_Final_out),
    .Q(j_k_ff_2_q), .Qn(j_k_ff_2_qn), .reset(not_2_out));  // open: preset
  not not_2 (not_2_out, On_Off_Indicator_Final);
  and and_3 (and_3_out, On_Off_Indicator_Final, Volume_Up_Final_out);
  and and_4 (and_4_out, On_Off_Indicator_Final, Volume_Down_Final_out);
  and and_5 (and_5_out, On_Off_Indicator_Final, j_k_ff_2_q);
  and and_6 (and_6_out, j_k_ff_2_qn, On_Off_Indicator_Final);
  or or_1 (or_1_out, and_37_out, and_49_out);
  D_Flip_Flop d_ff_1 (.Q(d_ff_1_q), .preset(and_3_out), .reset(and_4_out));  // open: D, clk, Qn
  D_Flip_Flop d_ff_2 (
    .Q(d_ff_2_q), .preset(Next_Track_Final_out), .reset(Previous_Track_Final_out));  // open: D, clk, Qn
  or or_2 (or_2_out, Next_Track_Final_out, Previous_Track_Final_out);
  not not_3 (not_3_out, d_ff_1_q);
  not not_4 (not_4_out, or_23_out);
  not not_5 (not_5_out, d_ff_2_q);
  and and_7 (and_7_out, On_Off_Indicator_Final, d_ff_1_q);
  and and_8 (and_8_out, not_3_out, d_ff_4_q);
  and and_9 (and_9_out, d_ff_3_q, d_ff_1_q);
  and and_10 (and_10_out, not_3_out, d_ff_5_q);
  and and_11 (and_11_out, d_ff_4_q, d_ff_1_q);
  and and_12 (and_12_out, not_3_out, d_ff_6_q);
  and and_13 (and_13_out, d_ff_5_q, d_ff_1_q);
  and and_14 (and_14_out, not_3_out, d_ff_7_q);
  and and_15 (and_15_out, d_ff_6_q, d_ff_1_q);
  and and_16 (and_16_out, not_3_out, d_ff_8_q);
  and and_17 (and_17_out, d_ff_7_q, d_ff_1_q);
  and and_18 (and_18_out, not_3_out, d_ff_9_q);
  and and_19 (and_19_out, d_ff_8_q, d_ff_1_q);
  and and_20 (and_20_out, not_3_out, d_ff_10_q);
  and and_21 (and_21_out, d_ff_9_q, d_ff_1_q);
  and and_22 (and_22_out, not_3_out, in_3);
  or or_3 (or_3_out, and_40_out, and_23_out);
  and and_23 (and_23_out, not_4_out, not_5_out);
  xnor xnor_1 (xnor_1_out, and_3_out, and_4_out);
  or or_4 (or_4_out, and_7_out, and_8_out);
  or or_5 (or_5_out, and_9_out, and_10_out);
  or or_6 (or_6_out, and_11_out, and_12_out);
  or or_7 (or_7_out, and_13_out, and_14_out);
  or or_8 (or_8_out, and_15_out, and_16_out);
  or or_9 (or_9_out, and_17_out, and_18_out);
  or or_10 (or_10_out, and_19_out, and_20_out);
  or or_11 (or_11_out, and_21_out, and_22_out);
  J_K_Flip_Flop #(.trigger("falling")) j_k_ff_3 (
    .J(On_Off_Indicator_Final), .K(On_Off_Indicator_Final), .clk(or_2_out), .Q(j_k_ff_3_q[0]),
    .Qn(j_k_ff_3_qn), .preset(or_1_out), .reset(and_36_out));
  J_K_Flip_Flop #(.trigger("falling")) j_k_ff_4 (
    .J(On_Off_Indicator_Final), .K(On_Off_Indicator_Final), .clk(or_3_out), .Q(j_k_ff_4_q[0]),
    .Qn(j_k_ff_4_qn), .reset(and_37_out));  // open: preset
  D_Flip_Flop d_ff_3 (.D(or_4_out), .clk(xnor_1_out), .Q(d_ff_3_q));  // open: Qn, preset, reset
  D_Flip_Flop d_ff_4 (.D(or_5_out), .clk(xnor_1_out), .Q(d_ff_4_q));  // open: Qn, preset, reset
  D_Flip_Flop d_ff_5 (.D(or_6_out), .clk(xnor_1_out), .Q(d_ff_5_q));  // open: Qn, preset, reset
  D_Flip_Flop d_ff_6 (.D(or_7_out), .clk(xnor_1_out), .Q(d_ff_6_q));  // open: Qn, preset, reset
  D_Flip_Flop d_ff_7 (.D(or_8_out), .clk(xnor_1_out), .Q(d_ff_7_q));  // open: Qn, preset, reset
  D_Flip_Flop d_ff_8 (.D(or_9_out), .clk(xnor_1_out), .Q(d_ff_8_q));  // open: Qn, preset, reset
  D_Flip_Flop d_ff_9 (.D(or_10_out), .clk(xnor_1_out), .Q(d_ff_9_q));  // open: Qn, preset, reset
  D_Flip_Flop d_ff_10 (.D(or_11_out), .clk(xnor_1_out), .Q(d_ff_10_q));  // open: Qn, preset, reset
  not not_6 (not_6_out, d_ff_2_q);
  not not_7 (not_7_out, d_ff_2_q);
  and and_24 (and_24_out, d_ff_2_q, j_k_ff_3_q[0]);
  and and_25 (and_25_out, j_k_ff_3_qn, not_6_out);
  and and_26 (and_26_out, d_ff_2_q, j_k_ff_4_q[0]);
  and and_27 (and_27_out, j_k_ff_4_qn, not_7_out);
  J_K_Flip_Flop #(.trigger("falling")) j_k_ff_5 (
    .J(or_12_out), .K(or_12_out), .clk(or_2_out), .Q(j_k_ff_3_q[1]), .Qn(j_k_ff_5_qn), .reset(or_14_out));  // open: preset
  or or_12 (or_12_out, and_24_out, and_25_out);
  J_K_Flip_Flop #(.trigger("falling")) j_k_ff_6 (
    .J(or_13_out), .K(or_13_out), .clk(or_3_out), .Q(j_k_ff_4_q[1]), .Qn(j_k_ff_6_qn), .reset(or_15_out));  // open: preset
  or or_13 (or_13_out, and_26_out, and_27_out);
  or or_14 (or_14_out, and_38_out, and_36_out);
  or or_15 (or_15_out, and_39_out, and_37_out);
  and and_28 (and_28_out, and_24_out, j_k_ff_3_q[1]);
  and and_29 (and_29_out, j_k_ff_5_qn, and_25_out);
  and and_30 (and_30_out, and_26_out, j_k_ff_4_q[1]);
  and and_31 (and_31_out, j_k_ff_6_qn, and_27_out);
  or or_16 (or_16_out, and_28_out, and_29_out);
  or or_17 (or_17_out, and_30_out, and_31_out);
  J_K_Flip_Flop #(.trigger("falling")) j_k_ff_7 (
    .J(or_16_out), .K(or_16_out), .clk(or_2_out), .Q(j_k_ff_3_q[2]), .Qn(j_k_ff_7_qn), .reset(or_18_out));  // open: preset
  or or_18 (or_18_out, and_38_out, and_36_out);
  J_K_Flip_Flop #(.trigger("falling")) j_k_ff_8 (
    .J(or_17_out), .K(or_17_out), .clk(or_3_out), .Q(j_k_ff_4_q[2]), .Qn(j_k_ff_8_qn), .reset(or_19_out));  // open: preset
  or or_19 (or_19_out, and_39_out, and_37_out);
  and and_32 (and_32_out, and_28_out, j_k_ff_3_q[2]);
  and and_33 (and_33_out, j_k_ff_7_qn, and_29_out);
  and and_34 (and_34_out, and_30_out, j_k_ff_4_q[2]);
  and and_35 (and_35_out, j_k_ff_8_qn, and_31_out);
  J_K_Flip_Flop #(.trigger("falling")) j_k_ff_9 (
    .J(or_20_out), .K(or_20_out), .clk(or_2_out), .Q(j_k_ff_3_q[3]), .preset(and_49_out), .reset(and_36_out));  // open: Qn
  or or_20 (or_20_out, and_32_out, and_33_out);
  J_K_Flip_Flop #(.trigger("falling")) j_k_ff_10 (
    .J(or_21_out), .K(or_21_out), .clk(or_3_out), .Q(j_k_ff_4_q[3]), .reset(and_37_out));  // open: Qn, preset
  or or_21 (or_21_out, and_34_out, and_35_out);
  not not_8 (not_8_out, j_k_ff_3_q[2]);
  not not_9 (not_9_out, j_k_ff_3_q[0]);
  and and_36 (and_36_out, j_k_ff_3_q[3], not_8_out, d_ff_2_q, not_9_out, j_k_ff_3_q[1]);
  and and_37 (and_37_out, j_k_ff_4_q[3], d_ff_2_q, j_k_ff_4_q[1]);
  and and_38 (and_38_out, j_k_ff_3_q[3], j_k_ff_3_q[1], j_k_ff_3_q[0]);
  or or_22 (or_22_out, j_k_ff_4_q[1], j_k_ff_4_q[2]);
  and and_39 (and_39_out, j_k_ff_4_q[3], or_22_out, j_k_ff_4_q[0]);
  LED Play_LED_Final (.in(and_5_out));
  LED Pause_LED_Final (.in(and_6_out));
  and and_40 (and_40_out, j_k_ff_3_q[0], d_ff_2_q, j_k_ff_3_q[3]);
  and and_41 (and_41_out, On_Off_Indicator_Final, d_ff_3_q);
  or or_23 (or_23_out, j_k_ff_3_q[0], j_k_ff_3_q[1], j_k_ff_3_q[2], j_k_ff_3_q[3]);
  LedBar VOLUME (
    .led0(and_41_out), .led1(and_42_out), .led2(and_43_out), .led3(and_44_out), .led4(and_45_out),
    .led5(and_46_out), .led6(and_47_out), .led7(and_48_out));
  and and_42 (and_42_out, On_Off_Indicator_Final, d_ff_4_q);
  and and_43 (and_43_out, On_Off_Indicator_Final, d_ff_5_q);
  and and_44 (and_44_out, On_Off_Indicator_Final, d_ff_6_q);
  Hex_Digit_Display TRACK (.value(j_k_ff_4_q));  // open: dp
  and and_45 (and_45_out, On_Off_Indicator_Final, d_ff_7_q);
  and and_46 (and_46_out, On_Off_Indicator_Final, d_ff_8_q);
  Hex_Digit_Display hex_digit_display_1 (.value(j_k_ff_3_q));  // open: dp
  and and_47 (and_47_out, On_Off_Indicator_Final, d_ff_9_q);
  and and_48 (and_48_out, On_Off_Indicator_Final, d_ff_10_q);
  not not_10 (not_10_out, j_k_ff_3_q[0]);
  not not_11 (not_11_out, j_k_ff_3_q[1]);
  not not_12 (not_12_out, j_k_ff_3_q[2]);
  not not_13 (not_13_out, j_k_ff_3_q[3]);
  and and_49 (and_49_out, not_10_out, not_11_out, not_12_out, not_13_out, not_14_out, not_15_out, not_16_out, not_17_out);
  not not_14 (not_14_out, j_k_ff_4_q[0]);
  not not_15 (not_15_out, j_k_ff_4_q[1]);
  not not_16 (not_16_out, j_k_ff_4_q[2]);
  not not_17 (not_17_out, j_k_ff_4_q[3]);
endmodule
