// Logisim project circuit.circ as structural Verilog: 1 circuit, main circuit main
module main (
  input  input_A,
  input  input_B,
  input  input_A_2,
  input  input_B_2,
  input  input_A_3,
  input  input_B_3,
  input  input_A_4,
  input  input_B_4
);

  wire and_1_out, and_2_out, and_3_out, and_4_out, and_5_out, and_6_out, and_7_out, or_1_out, or_2_out,
       or_3_out, xor_1_out, xor_2_out, xor_3_out, xor_4_out, xor_5_out, xor_6_out, xor_7_out;

  and and_1 (and_1_out, input_A, input_B);
  xor xor_1 (xor_1_out, input_A_2, input_B_2);
  and and_2 (and_2_out, input_A_2, input_B_2);
  xor xor_2 (xor_2_out, input_A_3, input_B_3);
  and and_3 (and_3_out, input_A_3, input_B_3);
  xor xor_3 (xor_3_out, input_A_4, input_B_4);
  and and_4 (and_4_out, input_A_4, input_B_4);
  xor xor_4 (xor_4_out, input_A, input_B);
  xor xor_5 (xor_5_out, and_1_out, xor_1_out);
  and and_5 (and_5_out, and_1_out, xor_1_out);
  and and_6 (and_6_out, or_1_out, xor_2_out);
  and and_7 (and_7_out, or_2_out, xor_3_out);
  or or_1 (or_1_out, and_5_out, and_2_out);
  or or_2 (or_2_out, and_6_out, and_3_out);
  or or_3 (or_3_out, and_7_out, and_4_out);
  xor xor_6 (xor_6_out, or_1_out, xor_2_out);
  xor xor_7 (xor_7_out, or_2_out, xor_3_out);
  LED led_1 (.in(xor_4_out));
  LED led_2 (.in(xor_5_out));
  LED led_3 (.in(xor_6_out));
  LED led_4 (.in(xor_7_out));
  LED led_5 (.in(or_3_out));

  // Notes on the sheet:
  //   output bit 1 (Co)
  //   output bit 2 (Co)
  //   output bit 3 (Co)
  //   output bit 4 (carry to next 4-bit adder)
  //   Output bit 0
  //   Output bit 1
  //   Output bit 2
  //   Output bit 3
  //   least-significant bit (2^0)
  //   most-significant bit (2^3)
endmodule
