// Logisim project 3bits_countingUp.circ as structural Verilog: 1 circuit, main circuit main
module main (
  input  in_1,
  input  RS
);

  wire clock_1_out, j_k_ff_1_q, j_k_ff_2_q, j_k_ff_3_q;

  Clock clock_1 (.out(clock_1_out));
  J_K_Flip_Flop #(.trigger("falling")) j_k_ff_1 (
    .J(in_1), .K(in_1), .clk(clock_1_out), .Q(j_k_ff_1_q), .reset(RS));  // open: Qn, preset
  LED led_1 (.in(j_k_ff_1_q));
  J_K_Flip_Flop #(.trigger("falling")) j_k_ff_2 (
    .J(in_1), .K(in_1), .clk(j_k_ff_1_q), .Q(j_k_ff_2_q), .reset(RS));  // open: Qn, preset
  LED led_2 (.in(j_k_ff_2_q));
  J_K_Flip_Flop #(.trigger("falling")) j_k_ff_3 (
    .J(in_1), .K(in_1), .clk(j_k_ff_2_q), .Q(j_k_ff_3_q), .reset(RS));  // open: Qn, preset
  LED led_3 (.in(j_k_ff_3_q));

  // Notes on the sheet:
  //   big endian
endmodule
