// Logisim project CountingUpTo5.circ as structural Verilog: 1 circuit, main circuit main
module main (
  input  in_1,
  input  Reset,
  input  in_3,
  input  in_4,
  input  in_5,
  input  in_6,
  input  in_7,
  input  in_8
);

  wire and_1_out, and_2_out, and_3_out, and_4_out, and_5_out, clock_1_out, clock_2_out, clock_3_out,
       clock_4_out, j_k_ff_1_q, j_k_ff_2_q, j_k_ff_3_q, j_k_ff_4_q, j_k_ff_5_q, j_k_ff_6_q, j_k_ff_8_q,
       j_k_ff_10_q, j_k_ff_12_q, not_1_out, not_2_out;
  wire [2:0] d_ff_1_q, j_k_ff_7_q;

  J_K_Flip_Flop j_k_ff_1 (.J(in_1), .K(in_1), .clk(clock_1_out), .Q(j_k_ff_1_q), .reset(Reset));  // open: Qn, preset
  Clock clock_1 (.out(clock_1_out));
  Clock clock_2 (.out(clock_2_out));
  LED led_1 (.in(j_k_ff_1_q));
  J_K_Flip_Flop #(.trigger("falling")) j_k_ff_2 (
    .J(in_4), .K(in_4), .clk(clock_2_out), .Q(j_k_ff_2_q), .reset(in_5));  // open: Qn, preset
  J_K_Flip_Flop j_k_ff_3 (.J(in_1), .K(in_1), .clk(j_k_ff_1_q), .Q(j_k_ff_3_q), .reset(Reset));  // open: Qn, preset
  LED led_2 (.in(j_k_ff_2_q));
  LED led_3 (.in(j_k_ff_3_q));
  J_K_Flip_Flop #(.trigger("falling")) j_k_ff_4 (
    .J(j_k_ff_2_q), .K(j_k_ff_2_q), .clk(clock_2_out), .Q(j_k_ff_4_q), .reset(in_5));  // open: Qn, preset
  J_K_Flip_Flop j_k_ff_5 (.J(in_1), .K(in_1), .clk(j_k_ff_3_q), .Q(j_k_ff_5_q), .reset(Reset));  // open: Qn, preset
  LED led_4 (.in(j_k_ff_4_q));
  LED led_5 (.in(j_k_ff_5_q));
  and and_1 (and_1_out, j_k_ff_4_q, j_k_ff_2_q);
  J_K_Flip_Flop #(.trigger("falling")) j_k_ff_6 (
    .J(and_1_out), .K(and_1_out), .clk(clock_2_out), .Q(j_k_ff_6_q), .reset(in_5));  // open: Qn, preset
  LED led_6 (.in(j_k_ff_6_q));
  Clock clock_3 (.out(clock_3_out));
  Clock clock_4 (.out(clock_4_out));
  J_K_Flip_Flop j_k_ff_7 (
    .J(in_3), .K(in_3), .clk(clock_3_out), .Q(j_k_ff_7_q[0]), .reset(and_4_out));  // open: Qn, preset
  LED led_7 (.in(j_k_ff_7_q[0]));
  J_K_Flip_Flop j_k_ff_8 (
    .J(in_7), .K(in_7), .clk(clock_4_out), .Q(j_k_ff_8_q), .reset(and_5_out));  // open: Qn, preset
  LED led_8 (.in(j_k_ff_8_q));
  J_K_Flip_Flop j_k_ff_9 (
    .J(j_k_ff_7_q[0]), .K(j_k_ff_7_q[0]), .clk(clock_3_out), .Q(j_k_ff_7_q[1]), .reset(and_4_out));  // open: Qn, preset
  J_K_Flip_Flop j_k_ff_10 (
    .J(j_k_ff_8_q), .K(j_k_ff_8_q), .clk(clock_4_out), .Q(j_k_ff_10_q), .reset(and_5_out));  // open: Qn, preset
  D_Flip_Flop d_ff_1 (.D(j_k_ff_8_q), .clk(clock_4_out), .Q(d_ff_1_q[0]));  // open: Qn, preset, reset
  LED led_9 (.in(j_k_ff_7_q[1]));
  LED led_10 (.in(j_k_ff_10_q));
  and and_2 (and_2_out, j_k_ff_7_q[1], j_k_ff_7_q[0]);
  J_K_Flip_Flop j_k_ff_11 (
    .J(and_2_out), .K(and_2_out), .clk(clock_3_out), .Q(j_k_ff_7_q[2]), .reset(and_4_out));  // open: Qn, preset
  and and_3 (and_3_out, j_k_ff_10_q, j_k_ff_8_q);
  LED led_11 (.in(j_k_ff_7_q[2]));
  Hex_Digit_Display hex_digit_display_1 (.value({in_6, j_k_ff_7_q}));  // open: dp
  J_K_Flip_Flop j_k_ff_12 (
    .J(and_3_out), .K(and_3_out), .clk(clock_4_out), .Q(j_k_ff_12_q), .reset(and_5_out));  // open: Qn, preset
  D_Flip_Flop d_ff_2 (.D(j_k_ff_10_q), .clk(clock_4_out), .Q(d_ff_1_q[1]));  // open: Qn, preset, reset
  Hex_Digit_Display hex_digit_display_2 (.value({in_8, d_ff_1_q}));  // open: dp
  and and_4 (and_4_out, j_k_ff_7_q[1], not_1_out, j_k_ff_7_q[2]);
  and and_5 (and_5_out, j_k_ff_10_q, not_2_out, j_k_ff_12_q);
  LED led_12 (.in(j_k_ff_12_q));
  not not_1 (not_1_out, j_k_ff_7_q[0]);
  not not_2 (not_2_out, j_k_ff_8_q);
  D_Flip_Flop d_ff_3 (.D(j_k_ff_12_q), .clk(clock_4_out), .Q(d_ff_1_q[2]));  // open: Qn, preset, reset

  // Notes on the sheet:
  //   Counting Up Ribble Clock
  //   Counting Up Common Clock
  //   1
  //   1
  //   2
  //   2
  //   4
  //   4
  //   Counting Up Common Clock to 5 illegal
  //   1
  //   Counting Up Common Clock to 5
  //   2
  //   4
endmodule
