// Logisim project HEXdigit.circ as structural Verilog: 1 circuit, main circuit main
module main (
  input  in_1
);

  wire clock_1_out;
  wire [3:0] j_k_ff_1_q;

  Clock clock_1 (.out(clock_1_out));
  J_K_Flip_Flop #(.trigger("falling")) j_k_ff_1 (
    .J(1'b1), .K(1'b1), .clk(clock_1_out), .Q(j_k_ff_1_q[0]), .reset(in_1));  // open: Qn, preset
  LED led_1 (.in(j_k_ff_1_q[0]));
  J_K_Flip_Flop #(.trigger("falling")) j_k_ff_2 (
    .J(1'b1), .K(1'b1), .clk(j_k_ff_1_q[0]), .Q(j_k_ff_1_q[1]), .reset(in_1));  // open: Qn, preset
  LED led_2 (.in(j_k_ff_1_q[1]));
  LED led_3 (.in(j_k_ff_1_q[2]));
  J_K_Flip_Flop #(.trigger("falling")) j_k_ff_3 (
    .J(1'b1), .K(1'b1), .clk(j_k_ff_1_q[1]), .Q(j_k_ff_1_q[2]), .reset(in_1));  // open: Qn, preset
  J_K_Flip_Flop #(.trigger("falling")) j_k_ff_4 (
    .J(1'b1), .K(1'b1), .clk(j_k_ff_1_q[2]), .Q(j_k_ff_1_q[3]), .reset(in_1));  // open: Qn, preset
  LED led_4 (.in(j_k_ff_1_q[3]));
  Hex_Digit_Display hex_digit_display_1 (.value(j_k_ff_1_q));  // open: dp
endmodule
