// Logisim project ReviewingAdder.circ as structural Verilog: 1 circuit, main circuit main
module main (
  input  input_1,
  input  input_2,
  input  in_3,
  input  in_4,
  input  in_5
);

  wire and_1_out, and_2_out, and_3_out, xor_1_out, xor_2_out, xor_3_out;

  xor xor_1 (xor_1_out, input_1, input_2);
  and and_1 (and_1_out, input_1, input_2);
  xor xor_2 (xor_2_out, in_4, in_5);
  and and_2 (and_2_out, in_4, in_5);
  LED led_1 (.in(xor_1_out));
  LED led_2 (.in(and_1_out));
  xor xor_3 (xor_3_out, in_3, xor_2_out);
  and and_3 (and_3_out, in_3, and_2_out);
  LED led_3 (.in(xor_3_out));
  LED led_4 (.in(and_3_out));

  // Notes on the sheet:
  //   Half-Adder
  //   Full-Adder
  //   carry in
  //   input 1
  //   input 2
  //   Output
  //   Carry-out
endmodule
