// Logisim project DFlipFlop.circ as structural Verilog: 1 circuit, main circuit main
module main (
  input  in_1,
  input  in_2,
  input  in_3
);

  wire and_1_out, and_2_out, button_1_out, button_2_out, button_3_out, clock_1_out, clock_2_out, clock_3_out,
       clock_4_out, d_ff_1_q, d_ff_1_qn, nand_1_out, nand_2_out, nand_3_out, nand_4_out, nor_1_out,
       nor_2_out, not_1_out, not_2_out, s_r_ff_1_q, s_r_ff_1_qn;

  Button button_1 (.out(button_1_out));
  Clock clock_1 (.out(clock_1_out));
  Clock clock_2 (.out(clock_2_out));
  not not_1 (not_1_out, button_1_out);
  not not_2 (not_2_out, in_3);
  nand nand_1 (nand_1_out, not_1_out, clock_1_out);
  nand nand_2 (nand_2_out, button_1_out, clock_1_out);
  and and_1 (and_1_out, not_2_out, clock_2_out);
  and and_2 (and_2_out, in_3, clock_2_out);
  nand nand_3 (nand_3_out, nand_1_out, nand_4_out);
  nand nand_4 (nand_4_out, nand_3_out, nand_2_out);
  nor nor_1 (nor_1_out, and_1_out, nor_2_out);
  nor nor_2 (nor_2_out, nor_1_out, and_2_out);
  LED led_1 (.in(nand_3_out));
  LED led_2 (.in(nand_4_out));
  LED led_3 (.in(nor_1_out));
  LED led_4 (.in(nor_2_out));
  Clock clock_3 (.out(clock_3_out));
  Button button_2 (.out(button_2_out));
  Button button_3 (.out(button_3_out));
  Clock clock_4 (.out(clock_4_out));
  D_Flip_Flop d_ff_1 (.D(in_1), .clk(clock_3_out), .Q(d_ff_1_q), .Qn(d_ff_1_qn), .reset(in_2));  // open: preset
  S_R_Flip_Flop s_r_ff_1 (
    .S(button_2_out), .R(button_3_out), .clk(clock_4_out), .Q(s_r_ff_1_q), .Qn(s_r_ff_1_qn));  // open: reset, preset
  LED led_5 (.in(d_ff_1_q));
  LED led_6 (.in(d_ff_1_qn));
  LED led_7 (.in(s_r_ff_1_q));
  LED led_8 (.in(s_r_ff_1_qn));

  // Notes on the sheet:
  //   D Flip Flop with NAND gate
  //   D Flip Flop with NOR gate
endmodule
