// Logisim project CircuitSelection.circ as structural Verilog: 1 circuit, main circuit main
module main (
  input  in_1,
  input  X,
  input  Y,
  input  A,
  input  B,
  input  in_6,
  input  Data,
  input  in_8
);

  wire and_1_out, and_2_out, and_3_out, and_4_out, and_5_out, and_6_out, clock_1_out, d_ff_1_q, d_ff_2_q,
       not_1_out, not_2_out, or_1_out, or_2_out, xor_1_out, xor_2_out;

  not not_1 (not_1_out, in_8);
  xor xor_1 (xor_1_out, X, Y);
  and and_1 (and_1_out, Data, not_1_out);
  and and_2 (and_2_out, in_8, Data);
  Clock clock_1 (.out(clock_1_out));
  not not_2 (not_2_out, in_6);
  D_Flip_Flop d_ff_1 (.D(and_2_out), .clk(clock_1_out), .Q(d_ff_1_q));  // open: Qn, preset, reset
  xor xor_2 (xor_2_out, in_1, xor_1_out);
  and and_3 (and_3_out, X, Y);
  and and_4 (and_4_out, in_1, xor_1_out);
  and and_5 (and_5_out, B, not_2_out);
  and and_6 (and_6_out, in_6, A);
  LED led_1 (.in(d_ff_1_q));
  LED led_2 (.in(xor_2_out));
  or or_1 (or_1_out, and_3_out, and_4_out);
  LED led_3 (.in(or_1_out));
  or or_2 (or_2_out, and_5_out, and_6_out);
  D_Flip_Flop d_ff_2 (.D(and_1_out), .clk(clock_1_out), .Q(d_ff_2_q));  // open: Qn, preset, reset
  LED led_4 (.in(or_2_out));
  LED led_5 (.in(d_ff_2_q));

  // Notes on the sheet:
  //   Carry In
  //   Activate L?
  //   Controlled Gate
  //   Select A, Deactivate B
  //   Selection Right Or Left
  //   R
  //   L
  //   Right will be choosen by default
endmodule
