// Logisim project CountingUpDown.circ as structural Verilog: 1 circuit, main circuit main
module main (
  input  in_1,
  input  in_2,
  input  Reset,
  input  Reset_2,
  input  in_5,
  input  in_6,
  input  in_7,
  input  Reset_3
);

  wire and_1_out, and_2_out, button_1_out, button_2_out, clock_1_out, clock_2_out, clock_3_out, j_k_ff_1_q,
       j_k_ff_2_q, j_k_ff_3_q, j_k_ff_4_q, j_k_ff_5_q, j_k_ff_6_q, j_k_ff_7_q, j_k_ff_8_q, j_k_ff_9_qn,
       j_k_ff_10_q, j_k_ff_11_qn;
  wire [2:0] j_k_ff_9_q;

  Clock clock_1 (.out(clock_1_out));
  Clock clock_2 (.out(clock_2_out));
  J_K_Flip_Flop j_k_ff_1 (.J(in_7), .K(in_7), .clk(clock_1_out), .Q(j_k_ff_1_q), .reset(Reset_3));  // open: Qn, preset
  LED led_1 (.in(j_k_ff_2_q));
  J_K_Flip_Flop j_k_ff_2 (.J(in_2), .K(in_2), .clk(clock_2_out), .Q(j_k_ff_2_q), .reset(Reset_2));  // open: Qn, preset
  LED led_2 (.in(j_k_ff_1_q));
  LED led_3 (.in(j_k_ff_3_q));
  J_K_Flip_Flop j_k_ff_3 (.J(in_2), .K(in_2), .clk(j_k_ff_2_q), .Q(j_k_ff_3_q), .reset(Reset_2));  // open: Qn, preset
  J_K_Flip_Flop j_k_ff_4 (
    .J(j_k_ff_1_q), .K(j_k_ff_1_q), .clk(clock_1_out), .Q(j_k_ff_4_q), .reset(Reset_3));  // open: Qn, preset
  LED led_4 (.in(j_k_ff_4_q));
  and and_1 (and_1_out, j_k_ff_1_q, j_k_ff_4_q);
  LED led_5 (.in(j_k_ff_5_q));
  J_K_Flip_Flop j_k_ff_5 (.J(in_2), .K(in_2), .clk(j_k_ff_3_q), .Q(j_k_ff_5_q), .reset(Reset_2));  // open: Qn, preset
  J_K_Flip_Flop j_k_ff_6 (
    .J(and_1_out), .K(and_1_out), .clk(clock_1_out), .Q(j_k_ff_6_q), .reset(Reset_3));  // open: Qn, preset
  LED led_6 (.in(j_k_ff_6_q));
  Clock clock_3 (.out(clock_3_out));
  J_K_Flip_Flop #(.trigger("falling")) j_k_ff_7 (
    .J(in_1), .K(in_1), .clk(clock_3_out), .Q(j_k_ff_7_q), .reset(Reset));  // open: Qn, preset
  LED led_7 (.in(j_k_ff_7_q));
  J_K_Flip_Flop #(.trigger("falling")) j_k_ff_8 (
    .J(in_1), .K(in_1), .clk(j_k_ff_7_q), .Q(j_k_ff_8_q), .reset(Reset));  // open: Qn, preset
  Button button_1 (.out(button_1_out));
  Button button_2 (.out(button_2_out));
  LED led_8 (.in(j_k_ff_8_q));
  J_K_Flip_Flop j_k_ff_9 (
    .J(in_6), .K(in_6), .clk(button_2_out), .Q(j_k_ff_9_q[0]), .Qn(j_k_ff_9_qn), .reset(button_1_out));  // open: preset
  J_K_Flip_Flop #(.trigger("falling")) j_k_ff_10 (
    .J(in_1), .K(in_1), .clk(j_k_ff_8_q), .Q(j_k_ff_10_q), .reset(Reset));  // open: Qn, preset
  LED led_9 (.in(j_k_ff_10_q));
  J_K_Flip_Flop j_k_ff_11 (
    .J(j_k_ff_9_qn), .K(j_k_ff_9_qn), .clk(button_2_out), .Q(j_k_ff_9_q[1]), .Qn(j_k_ff_11_qn),
    .reset(button_1_out));  // open: preset
  J_K_Flip_Flop j_k_ff_12 (
    .J(and_2_out), .K(and_2_out), .clk(button_2_out), .Q(j_k_ff_9_q[2]), .reset(button_1_out));  // open: Qn, preset
  and and_2 (and_2_out, j_k_ff_11_qn, j_k_ff_9_qn);
  Hex_Digit_Display hex_digit_display_1 (.value({in_5, j_k_ff_9_q}));  // open: dp

  // Notes on the sheet:
  //   Asynchronous Circuit Counting Down 
  //   1
  //   Synchronous Circuit Counting Up
  //   1
  //   2
  //   2
  //   4
  //   4
  //   1
  //   Asynchronous Circuit Counting Up
  //   Synchronous Circuit Counting Down
  //   2
  //   4
endmodule
