// Logisim project Stack.circ as structural Verilog: 1 circuit, main circuit main
module main (
  input  in_1,
  input  in_2,
  input  in_3,
  input  in_4
);

  wire clock_1_out, clock_2_out, d_ff_1_q, d_ff_2_q, d_ff_3_q, d_ff_4_q, d_ff_5_q, d_ff_6_q, d_ff_7_q,
       d_ff_8_q;

  Clock clock_1 (.out(clock_1_out));
  Clock clock_2 (.out(clock_2_out));
  D_Flip_Flop d_ff_1 (.D(in_1), .clk(clock_1_out), .Q(d_ff_1_q), .reset(in_2));  // open: Qn, preset
  D_Flip_Flop d_ff_2 (.D(d_ff_4_q), .clk(clock_2_out), .Q(d_ff_2_q), .reset(in_4));  // open: Qn, preset
  LED led_1 (.in(d_ff_1_q));
  LED led_2 (.in(d_ff_2_q));
  D_Flip_Flop d_ff_3 (.D(d_ff_1_q), .clk(clock_1_out), .Q(d_ff_3_q), .reset(in_2));  // open: Qn, preset
  D_Flip_Flop d_ff_4 (.D(d_ff_6_q), .clk(clock_2_out), .Q(d_ff_4_q), .reset(in_4));  // open: Qn, preset
  LED led_3 (.in(d_ff_3_q));
  LED led_4 (.in(d_ff_4_q));
  D_Flip_Flop d_ff_5 (.D(d_ff_3_q), .clk(clock_1_out), .Q(d_ff_5_q), .reset(in_2));  // open: Qn, preset
  D_Flip_Flop d_ff_6 (.D(d_ff_8_q), .clk(clock_2_out), .Q(d_ff_6_q), .reset(in_4));  // open: Qn, preset
  LED led_5 (.in(d_ff_5_q));
  LED led_6 (.in(d_ff_6_q));
  D_Flip_Flop d_ff_7 (.D(d_ff_5_q), .clk(clock_1_out), .Q(d_ff_7_q), .reset(in_2));  // open: Qn, preset
  D_Flip_Flop d_ff_8 (.D(in_3), .clk(clock_2_out), .Q(d_ff_8_q), .reset(in_4));  // open: Qn, preset
  LED led_7 (.in(d_ff_7_q));
  LED led_8 (.in(d_ff_8_q));

  // Notes on the sheet:
  //   Stack
  //   This circuit goes backward shift-left
endmodule
