// Logisim project draft.circ as structural Verilog: 1 circuit, main circuit main
module main (
  input  Set,
  input  Reset,
  input  D,
  input  J,
  input  K
);

  wire and_1_out, and_2_out, button_1_out, button_2_out, clock_1_out, clock_2_out, nand_1_out, nand_2_out,
       nand_3_out, nand_4_out, nor_1_out, nor_2_out, nor_3_out, nor_4_out, nor_5_out, nor_6_out, not_1_out;

  Clock clock_1 (.out(clock_1_out));
  Clock clock_2 (.out(clock_2_out));
  not not_1 (not_1_out, D);
  nand nand_1 (nand_1_out, nand_4_out, J, clock_2_out);
  nand nand_2 (nand_2_out, clock_2_out, K, nand_3_out);
  and and_1 (and_1_out, clock_1_out, not_1_out);
  and and_2 (and_2_out, clock_1_out, D);
  nand nand_3 (nand_3_out, nand_1_out, nand_4_out);
  nand nand_4 (nand_4_out, nand_3_out, nand_2_out);
  nor nor_1 (nor_1_out, and_1_out, nor_2_out);
  nor nor_2 (nor_2_out, nor_1_out, and_2_out);
  LED led_1 (.in(nand_3_out));
  LED led_2 (.in(nand_4_out));
  LED led_3 (.in(nor_1_out));
  LED led_4 (.in(nor_2_out));
  Button button_1 (.out(button_1_out));
  Button button_2 (.out(button_2_out));
  nor nor_3 (nor_3_out, Set, nor_4_out);
  nor nor_4 (nor_4_out, nor_3_out, Reset);
  nor nor_5 (nor_5_out, button_1_out, nor_6_out);
  nor nor_6 (nor_6_out, nor_5_out, button_2_out);
  LED led_5 (.in(nor_3_out));
  LED led_6 (.in(nor_4_out));
  LED led_7 (.in(nor_5_out));
  LED led_8 (.in(nor_6_out));

  // Notes on the sheet:
  //   Q
  //   Q'
  //   Reset
  //   Set
  //   Q
  //   Q'
endmodule
